// Logisim project DFF_enable.circ as structural Verilog: 4 circuits, main circuit D_Latch
module main (
  input  EN,
  input  D,
  output Q
);

  wire multiplexer_1_out;

  Multiplexer multiplexer_1 (.in0(Q), .in1(D), .out(multiplexer_1_out), .sel(EN));
  DFF1 dff1_1 (.D(multiplexer_1_out), .Reset(1'b1), .Q(Q));  // open: QQ
endmodule

module D_Latch (
  input  WE,
  input  D,
  output Q,
  output QQ
);

  wire and_1_out, and_2_out, not_1_out;

  not not_1 (not_1_out, D);
  and and_1 (and_1_out, D, WE);
  and and_2 (and_2_out, WE, not_1_out);
  RS_Latch rs_latch_1 (.R(and_2_out), .S(and_1_out), .Q(Q), .QQ(QQ));
endmodule

module RS_Latch (
  input  R,
  input  S,
  output Q,
  output QQ
);

  nor nor_1 (Q, R, QQ);
  nor nor_2 (QQ, Q, S);
endmodule

module DFF1 (
  input  D,
  input  Reset,
  output Q,
  output QQ
);

  wire and_1_out, clock_1_out, d_latch_1_q, not_1_out;

  Clock clock_1 (.out(clock_1_out));
  not not_1 (not_1_out, clock_1_out);
  and and_1 (and_1_out, D, Reset);
  D_Latch d_latch_1 (.WE(not_1_out), .D(and_1_out), .Q(d_latch_1_q));  // open: QQ
  D_Latch d_latch_2 (.WE(clock_1_out), .D(d_latch_1_q), .Q(Q), .QQ(QQ));
endmodule
