// Logisim project D_Latch.circ as structural Verilog
module main (
  input  D,
  input  WE,
  output Q,
  output out_4
);

  wire and_1_out, and_2_out, and_3_out, dipswitch_1_sw1, not_1_out, not_2_out, or_1_out;

  DipSwitch #(.number(1)) dipswitch_1 (.sw1(dipswitch_1_sw1));
  not not_1 (not_1_out, D);
  and and_1 (and_1_out, WE, not_1_out);
  not not_2 (not_2_out, dipswitch_1_sw1);
  or or_1 (or_1_out, dipswitch_1_sw1, and_1_out);
  and and_2 (and_2_out, D, WE);
  and and_3 (and_3_out, and_2_out, not_2_out);
  nor nor_1 (Q, or_1_out, out_4);
  nor nor_2 (out_4, Q, and_3_out);
endmodule
