// Logisim project SR_Latch.circ as structural Verilog: 1 circuit, main circuit main
module main (
  input  in_1,
  input  in_2,
  input  S,
  input  R,
  output Q,
  output QQ,
  output Q1,
  output out_8
);

  wire and_1_out, and_2_out, dipswitch_1_sw1, not_1_out, not_2_out;

  DipSwitch #(.number(1)) dipswitch_1 (.sw1(dipswitch_1_sw1));
  and and_1 (and_1_out, in_1, dipswitch_1_sw1);
  and and_2 (and_2_out, dipswitch_1_sw1, in_2);
  not not_1 (not_1_out, S);
  not not_2 (not_2_out, R);
  nor nor_1 (Q, and_1_out, QQ);
  nor nor_2 (QQ, Q, and_2_out);
  nand nand_1 (Q1, not_1_out, out_8);
  nand nand_2 (out_8, Q1, not_2_out);
endmodule
