// Logisim project Sum(digital).circ as structural Verilog: 1 circuit, main circuit main
module main (
  input  RESET
);

  wire clock_1_out, comparator_1_eq, comparator_1_lt, or_1_out;
  wire [3:0] adder_1_out, adder_1_out_2;
  wire [7:0] adder_2_out, register_1_q, register_2_q;

  Clock clock_1 (.out(clock_1_out));
  Register register_1 (
    .D({adder_1_out_2, adder_1_out}), .en(or_1_out), .clk(clock_1_out), .Q(register_1_q), .clr(RESET));
  Adder adder_1 (.a(register_1_q), .b(8'h1), .out({adder_1_out_2, adder_1_out}));  // open: cin, cout
  Register register_2 (.D(adder_2_out), .en(or_1_out), .clk(clock_1_out), .Q(register_2_q), .clr(RESET));
  Hex_Digit_Display hex_digit_display_1 (.value(adder_1_out_2));  // open: dp
  Adder adder_2 (.a({adder_1_out_2, adder_1_out}), .b(register_2_q), .out(adder_2_out));  // open: cin, cout
  Hex_Digit_Display hex_digit_display_2 (.value(adder_1_out));  // open: dp
  Comparator comparator_1 (
    .a({adder_1_out_2, adder_1_out}), .b(8'ha), .eq(comparator_1_eq), .lt(comparator_1_lt));  // open: gt
  Hex_Digit_Display hex_digit_display_3 (.value(register_2_q[7:4]));  // open: dp
  or or_1 (or_1_out, comparator_1_eq, comparator_1_lt);
  Hex_Digit_Display hex_digit_display_4 (.value(register_2_q[3:0]));  // open: dp
endmodule
