// Logisim project adder_4bit.circ as structural Verilog: 3 circuits, main circuit main
module main (
  input  [3:0] A,
  input  [3:0] B
);

  wire full_adder_1_cout, full_adder_2_cout, full_adder_3_cout, full_adder_4_cout, not_1_out, not_2_out,
       not_3_out, not_4_out, not_5_out;
  wire [3:0] full_adder_1_s;

  not not_1 (not_1_out, B[0]);
  not not_2 (not_2_out, B[1]);
  full_adder full_adder_1 (.A(A[0]), .B(not_1_out), .Cin(1'b1), .S(full_adder_1_s[0]), .Cout(full_adder_1_cout));
  full_adder full_adder_2 (
    .A(A[1]), .B(not_2_out), .Cin(full_adder_1_cout), .S(full_adder_1_s[1]), .Cout(full_adder_2_cout));
  not not_3 (not_3_out, B[2]);
  not not_4 (not_4_out, B[3]);
  full_adder full_adder_3 (
    .A(A[2]), .B(not_3_out), .Cin(full_adder_2_cout), .S(full_adder_1_s[2]), .Cout(full_adder_3_cout));
  Hex_Digit_Display hex_digit_display_1 (.value(full_adder_1_s));  // open: dp
  full_adder full_adder_4 (
    .A(A[3]), .B(not_4_out), .Cin(full_adder_3_cout), .S(full_adder_1_s[3]), .Cout(full_adder_4_cout));
  not not_5 (not_5_out, full_adder_4_cout);
  LED led_1 (.in(not_5_out));
endmodule

module half_adder (
  input  in_1,
  input  in_2,
  output S,
  output C
);

  xor xor_1 (S, in_1, in_2);
  and and_1 (C, in_1, in_2);
endmodule

module full_adder (
  input  A,
  input  B,
  input  Cin,
  output S,
  output Cout
);

  wire half_adder_1_c, half_adder_1_s, half_adder_2_c;

  half_adder half_adder_1 (.in_1(A), .in_2(B), .S(half_adder_1_s), .C(half_adder_1_c));
  half_adder half_adder_2 (.in_1(half_adder_1_s), .in_2(Cin), .S(S), .C(half_adder_2_c));
  or or_1 (Cout, half_adder_2_c, half_adder_1_c);
endmodule
