// Logisim project counter4.circ as structural Verilog: 4 circuits, main circuit D_Latch
module main (
  input  RESET
);

  wire clock_1_out;
  wire [3:0] adder_1_out, dff1_1_q;

  Clock clock_1 (.out(clock_1_out));
  DFF1 dff1_1 (.Clk(clock_1_out), .D(adder_1_out[0]), .Reset(RESET), .Q(dff1_1_q[0]));  // open: QQ
  DFF1 dff1_2 (.Clk(clock_1_out), .D(adder_1_out[1]), .Reset(RESET), .Q(dff1_1_q[1]));  // open: QQ
  DFF1 dff1_3 (.Clk(clock_1_out), .D(adder_1_out[2]), .Reset(RESET), .Q(dff1_1_q[2]));  // open: QQ
  DFF1 dff1_4 (.Clk(clock_1_out), .D(adder_1_out[3]), .Reset(RESET), .Q(dff1_1_q[3]));  // open: QQ
  Hex_Digit_Display hex_digit_display_1 (.value(dff1_1_q));  // open: dp
  Adder #(.width(4)) adder_1 (.a(dff1_1_q), .b(4'b0001), .out(adder_1_out));  // open: cin, cout
endmodule

module D_Latch (
  input  WE,
  input  D,
  output Q,
  output QQ
);

  wire and_1_out, and_2_out, not_1_out;

  not not_1 (not_1_out, D);
  and and_1 (and_1_out, D, WE);
  and and_2 (and_2_out, WE, not_1_out);
  RS_Latch rs_latch_1 (.R(and_2_out), .S(and_1_out), .Q(Q), .QQ(QQ));
endmodule

module RS_Latch (
  input  R,
  input  S,
  output Q,
  output QQ
);

  nor nor_1 (Q, R, QQ);
  nor nor_2 (QQ, Q, S);
endmodule

module DFF1 (
  input  Clk,
  input  D,
  input  Reset,
  output Q,
  output QQ
);

  wire and_1_out, d_latch_1_q, not_1_out;

  not not_1 (not_1_out, Clk);
  and and_1 (and_1_out, D, Reset);
  D_Latch d_latch_1 (.WE(not_1_out), .D(and_1_out), .Q(d_latch_1_q));  // open: QQ
  D_Latch d_latch_2 (.WE(Clk), .D(d_latch_1_q), .Q(Q), .QQ(QQ));
endmodule
