// Logisim project decoder_expension.circ as structural Verilog: 3 circuits, main circuit main
module main (
  input  A0,
  input  A1,
  input  A2,
  input  in_4,
  input  in_5,
  input  in_6,
  output Y0,
  output Y1,
  output Y2,
  output Y3,
  output Y4,
  output Y5,
  output Y6,
  output Y7,
  output out_15,
  output out_16,
  output out_17,
  output out_18,
  output out_19,
  output out_20,
  output out_21,
  output out_22
);

  wire not_1_out, not_2_out, yimaqi_1_y0, yimaqi_1_y1, yimaqi_1_y2, yimaqi_1_y3;

  not not_1 (not_1_out, in_6);
  not not_2 (not_2_out, A0);
  yimaqi yimaqi_1 (
    .A0(A1), .A1(A2), .Y0(yimaqi_1_y0), .Y1(yimaqi_1_y1), .Y2(yimaqi_1_y2), .Y3(yimaqi_1_y3));  // open: En
  two_four_decoder_en two_four_decoder_en_1 (
    .A0(in_4), .A1(in_5), .En(not_1_out), .Y0(out_15), .Y1(out_16), .Y2(out_17), .Y3(out_18));
  two_four_decoder_en two_four_decoder_en_2 (
    .A0(in_4), .A1(in_5), .En(in_6), .Y0(out_19), .Y1(out_20), .Y2(out_21), .Y3(out_22));
  and and_1 (Y0, not_2_out, yimaqi_1_y0);
  and and_2 (Y1, A0, yimaqi_1_y0);
  and and_3 (Y2, yimaqi_1_y1, not_2_out);
  and and_4 (Y3, A0, yimaqi_1_y1);
  and and_5 (Y4, not_2_out, yimaqi_1_y2);
  and and_6 (Y5, A0, yimaqi_1_y2);
  and and_7 (Y6, not_2_out, yimaqi_1_y3);
  and and_8 (Y7, A0, yimaqi_1_y3);
endmodule

module yimaqi (
  input  A0,
  input  A1,
  input  En,
  output Y0,
  output Y1,
  output Y2,
  output Y3
);

  wire not_1_out, not_2_out;

  not not_1 (not_1_out, A0);
  not not_2 (not_2_out, A1);
  and and_1 (Y0, not_1_out, En, not_2_out);
  and and_2 (Y1, not_2_out, En, A0);
  and and_3 (Y2, not_1_out, En, A1);
  and and_4 (Y3, A0, En, A1);
endmodule

module two_four_decoder_en (
  input  A0,
  input  A1,
  input  En,
  output Y0,
  output Y1,
  output Y2,
  output Y3
);

  wire not_1_out, not_2_out;

  not not_1 (not_1_out, A0);
  not not_2 (not_2_out, A1);
  and and_1 (Y0, not_1_out, En, not_2_out);
  and and_2 (Y1, not_2_out, En, A0);
  and and_3 (Y2, not_1_out, En, A1);
  and and_4 (Y3, A0, En, A1);
endmodule
