// Logisim project digital_clock.circ as structural Verilog: 1 circuit, main circuit main
module main (
  input  RESET
);

  wire clock_1_out, comparator_1_gt, comparator_2_gt, comparator_3_gt, comparator_4_gt;
  wire [3:0] adder_1_out, adder_2_out, adder_3_out, adder_4_out, multiplexer_1_out, multiplexer_2_out,
       multiplexer_3_out, multiplexer_4_out, multiplexer_5_out, multiplexer_6_out, multiplexer_7_out,
       register_1_q, register_2_q, register_3_q, register_4_q;

  Register #(.width(4)) register_1 (.D(multiplexer_3_out), .en(1'b1), .clk(clock_1_out), .Q(register_1_q), .clr(RESET));
  Register #(.width(4)) register_2 (.D(multiplexer_4_out), .en(1'b1), .clk(clock_1_out), .Q(register_2_q), .clr(RESET));
  Multiplexer #(.width(4)) multiplexer_1 (.in0(4'b0000), .in1(4'b0001), .out(multiplexer_1_out), .sel(comparator_1_gt));
  Clock clock_1 (.out(clock_1_out));
  Adder #(.width(4)) adder_1 (.a(register_2_q), .b(multiplexer_2_out), .out(adder_1_out));  // open: cin, cout
  Multiplexer #(.width(4)) multiplexer_2 (.in0(4'b0000), .in1(4'b0001), .out(multiplexer_2_out), .sel(comparator_3_gt));
  Adder #(.width(4)) adder_2 (.a(register_1_q), .b(multiplexer_1_out), .out(adder_2_out));  // open: cin, cout
  Hex_Digit_Display hex_digit_display_1 (.value(register_1_q));  // open: dp
  Comparator #(.mode("unsigned"), .width(4)) comparator_1 (
    .a(adder_1_out), .b(4'b1001), .gt(comparator_1_gt));  // open: eq, lt
  Multiplexer #(.width(4)) multiplexer_3 (
    .in0(adder_2_out), .in1(4'b0000), .out(multiplexer_3_out), .sel(comparator_2_gt));
  Comparator #(.mode("unsigned"), .width(4)) comparator_2 (
    .a(adder_2_out), .b(4'b0101), .gt(comparator_2_gt));  // open: eq, lt
  Hex_Digit_Display hex_digit_display_2 (.value(register_2_q));  // open: dp
  Multiplexer #(.width(4)) multiplexer_4 (
    .in0(adder_1_out), .in1(4'b0000), .out(multiplexer_4_out), .sel(comparator_1_gt));
  Register #(.width(4)) register_3 (.D(multiplexer_6_out), .en(1'b1), .clk(clock_1_out), .Q(register_3_q), .clr(RESET));
  Hex_Digit_Display hex_digit_display_3 (.value(register_3_q));  // open: dp
  Hex_Digit_Display hex_digit_display_4 (.value(register_4_q));  // open: dp
  Register #(.width(4)) register_4 (.D(multiplexer_7_out), .en(1'b1), .clk(clock_1_out), .Q(register_4_q), .clr(RESET));
  Multiplexer #(.width(4)) multiplexer_5 (.in0(4'b0000), .in1(4'b0001), .out(multiplexer_5_out), .sel(comparator_4_gt));
  Adder #(.width(4)) adder_3 (.a(register_3_q), .b(multiplexer_5_out), .out(adder_3_out));  // open: cin, cout
  Adder #(.width(4)) adder_4 (.a(register_4_q), .b(4'b0001), .out(adder_4_out));  // open: cin, cout
  Multiplexer #(.width(4)) multiplexer_6 (
    .in0(adder_3_out), .in1(4'b0000), .out(multiplexer_6_out), .sel(comparator_3_gt));
  Comparator #(.mode("unsigned"), .width(4)) comparator_3 (
    .a(adder_3_out), .b(4'b0101), .gt(comparator_3_gt));  // open: eq, lt
  Comparator #(.mode("unsigned"), .width(4)) comparator_4 (
    .a(adder_4_out), .b(4'b1001), .gt(comparator_4_gt));  // open: eq, lt
  Multiplexer #(.width(4)) multiplexer_7 (
    .in0(adder_4_out), .in1(4'b0000), .out(multiplexer_7_out), .sel(comparator_4_gt));

  // Notes on the sheet:
  //   .
  //   .
endmodule
