// Logisim project digital_tube.circ as structural Verilog: 2 circuits, main circuit main
module main (
);

  wire and_1_out, dipswitch_1_p5, not_1_out, or_1_out, or_2_out, tube_decoder_1_a, tube_decoder_1_b,
       tube_decoder_1_c, tube_decoder_1_d, tube_decoder_1_e, tube_decoder_1_f, tube_decoder_1_g;
  wire [3:0] dipswitch_1_p1;

  // DipSwitch #(.number(5)) dipswitch_1: pin names not known; wires that end beside it: dipswitch_1_p1[0], dipswitch_1_p1[1], dipswitch_1_p1[2], dipswitch_1_p1[3], dipswitch_1_p5
  or or_1 (or_1_out, dipswitch_1_p1[1], dipswitch_1_p1[2]);
  and and_1 (and_1_out, or_1_out, dipswitch_1_p1[3]);
  not not_1 (not_1_out, and_1_out);
  or or_2 (or_2_out, not_1_out, dipswitch_1_p5);
  tube_decoder tube_decoder_1 (
    .EN(or_2_out), .in_2(dipswitch_1_p1), .G(tube_decoder_1_g), .A(tube_decoder_1_a), .B(tube_decoder_1_b),
    .F(tube_decoder_1_f), .E(tube_decoder_1_e), .C(tube_decoder_1_c), .D(tube_decoder_1_d));
  _7_Segment_Display u_7_segment_display_1 (
    .g(tube_decoder_1_g), .f(tube_decoder_1_f), .a(tube_decoder_1_a), .b(tube_decoder_1_b),
    .e(tube_decoder_1_e), .d(tube_decoder_1_d), .c(tube_decoder_1_c));  // open: dp
endmodule

module tube_decoder (
  input  EN,
  input  [3:0] in_2,
  output G,
  output A,
  output B,
  output F,
  output E,
  output C,
  output D
);

  wire decoder_1_out0, decoder_1_out1, decoder_1_out2, decoder_1_out3, decoder_1_out4, decoder_1_out5,
       decoder_1_out6, decoder_1_out7, decoder_1_out8, decoder_1_out9, decoder_1_out10, decoder_1_out11,
       decoder_1_out12, decoder_1_out13, decoder_1_out14, decoder_1_out15;

  Decoder #(.select(4)) decoder_1 (
    .out0(decoder_1_out0), .out1(decoder_1_out1), .out2(decoder_1_out2), .out3(decoder_1_out3),
    .out4(decoder_1_out4), .out5(decoder_1_out5), .out6(decoder_1_out6), .out7(decoder_1_out7),
    .out8(decoder_1_out8), .out9(decoder_1_out9), .out10(decoder_1_out10), .out11(decoder_1_out11),
    .out12(decoder_1_out12), .out13(decoder_1_out13), .out14(decoder_1_out14), .out15(decoder_1_out15),
    .sel(in_2), .en(EN));
  nor nor_1 (E, decoder_1_out1, decoder_1_out3, decoder_1_out4, decoder_1_out5, decoder_1_out7, decoder_1_out9);
  nor nor_2 (F, decoder_1_out1, decoder_1_out2, decoder_1_out13, decoder_1_out3, decoder_1_out7);
  nor nor_3 (A, decoder_1_out1, decoder_1_out11, decoder_1_out13, decoder_1_out4);
  nor nor_4 (B, decoder_1_out11, decoder_1_out5, decoder_1_out12, decoder_1_out14, decoder_1_out6, decoder_1_out15);
  nor nor_5 (D, decoder_1_out1, decoder_1_out10, decoder_1_out4, decoder_1_out15, decoder_1_out7);
  nor nor_6 (C, decoder_1_out2, decoder_1_out12, decoder_1_out14, decoder_1_out15);
  nor nor_7 (G, decoder_1_out0, decoder_1_out1, decoder_1_out7, decoder_1_out12);
endmodule
