// Logisim project encoder1.circ as structural Verilog: 2 circuits, main circuit main
module main (
);

  wire decoder_1_out0, decoder_1_out1, decoder_1_out2, decoder_1_out3, decoder_1_out4, decoder_1_out5,
       decoder_1_out6, decoder_1_out7, decoder_1_out8, decoder_1_out9, decoder_1_out10, decoder_1_out11,
       decoder_1_out12, decoder_1_out13, decoder_1_out14, decoder_1_out15, dipswitch_1_p1, dipswitch_1_p2,
       dipswitch_1_p3, dipswitch_1_p4, dipswitch_1_p5, dipswitch_1_p6, dipswitch_1_p7, dipswitch_1_p8,
       dipswitch_1_p9, dipswitch_1_p10, dipswitch_1_p11, dipswitch_1_p12, dipswitch_1_p13, dipswitch_1_p14,
       dipswitch_1_p15, dipswitch_1_p16, nor_1_out, nor_2_out, nor_3_out, nor_4_out, nor_5_out, nor_6_out,
       nor_7_out;
  wire [3:0] encoder1_1_y0;

  // DipSwitch #(.number(16)) dipswitch_1: pin names not known; wires that end beside it: dipswitch_1_p1, dipswitch_1_p2, dipswitch_1_p3, dipswitch_1_p4, dipswitch_1_p5, dipswitch_1_p6, dipswitch_1_p7, dipswitch_1_p8, dipswitch_1_p9, dipswitch_1_p10, dipswitch_1_p11, dipswitch_1_p12, dipswitch_1_p13, dipswitch_1_p14, dipswitch_1_p15, dipswitch_1_p16
  encoder1 encoder1_1 (
    .A0(dipswitch_1_p1), .A1(dipswitch_1_p2), .A2(dipswitch_1_p3), .A3(dipswitch_1_p4), .A4(dipswitch_1_p5),
    .A5(dipswitch_1_p6), .A6(dipswitch_1_p7), .A7(dipswitch_1_p8), .A8(dipswitch_1_p9), .A9(dipswitch_1_p10),
    .A10(dipswitch_1_p11), .A11(dipswitch_1_p12), .A12(dipswitch_1_p13), .A13(dipswitch_1_p14),
    .A14(dipswitch_1_p15), .A15(dipswitch_1_p16), .Y3(encoder1_1_y0[3]), .Y2(encoder1_1_y0[2]),
    .Y1(encoder1_1_y0[1]), .Y0(encoder1_1_y0[0]));
  Decoder #(.enable("false"), .select(4)) decoder_1 (
    .out0(decoder_1_out0), .out1(decoder_1_out1), .out2(decoder_1_out2), .out3(decoder_1_out3),
    .out4(decoder_1_out4), .out5(decoder_1_out5), .out6(decoder_1_out6), .out7(decoder_1_out7),
    .out8(decoder_1_out8), .out9(decoder_1_out9), .out10(decoder_1_out10), .out11(decoder_1_out11),
    .out12(decoder_1_out12), .out13(decoder_1_out13), .out14(decoder_1_out14), .out15(decoder_1_out15),
    .sel(encoder1_1_y0));
  nor nor_1 (nor_1_out, decoder_1_out1, decoder_1_out3, decoder_1_out4, decoder_1_out5, decoder_1_out7, decoder_1_out9);
  nor nor_2 (nor_2_out, decoder_1_out1, decoder_1_out2, decoder_1_out13, decoder_1_out3, decoder_1_out7);
  nor nor_3 (nor_3_out, decoder_1_out1, decoder_1_out11, decoder_1_out13, decoder_1_out4);
  nor nor_4 (nor_4_out, decoder_1_out11, decoder_1_out5, decoder_1_out12, decoder_1_out14, decoder_1_out6, decoder_1_out15);
  _7_Segment_Display u_7_segment_display_1 (
    .g(nor_7_out), .f(nor_2_out), .a(nor_3_out), .b(nor_4_out), .e(nor_1_out), .d(nor_5_out), .c(nor_6_out));  // open: dp
  nor nor_5 (nor_5_out, decoder_1_out1, decoder_1_out10, decoder_1_out4, decoder_1_out15, decoder_1_out7);
  nor nor_6 (nor_6_out, decoder_1_out2, decoder_1_out12, decoder_1_out14, decoder_1_out15);
  nor nor_7 (nor_7_out, decoder_1_out0, decoder_1_out1, decoder_1_out7, decoder_1_out12);
endmodule

module encoder1 (
  input  A0,
  input  A1,
  input  A2,
  input  A3,
  input  A4,
  input  A5,
  input  A6,
  input  A7,
  input  A8,
  input  A9,
  input  A10,
  input  A11,
  input  A12,
  input  A13,
  input  A14,
  input  A15,
  output Y3,
  output Y2,
  output Y1,
  output Y0
);

  or or_1 (Y3, A8, A9, A10, A11, A12, A13, A14, A15);
  or or_2 (Y2, A4, A5, A6, A7, A12, A13, A14, A15);
  or or_3 (Y1, A2, A3, A6, A7, A10, A11, A14, A15);
  or or_4 (Y0, A1, A3, A5, A7, A9, A11, A13, A15);
endmodule
