// Logisim project mux3_4_1.circ as structural Verilog: 1 circuit, main circuit main
module main (
  input  [2:0] in_1,
  input  [1:0] in_2,
  input  [2:0] in_3,
  input  [2:0] in_4,
  input  [2:0] in_5,
  output out_6,
  output out_7,
  output out_8
);

  wire and_1_out, and_2_out, and_3_out, and_4_out, and_5_out, and_6_out, and_7_out, and_8_out, and_9_out,
       and_10_out, and_11_out, and_12_out, decoder_1_out0, decoder_1_out1, decoder_1_out2, decoder_1_out3;

  Decoder #(.select(2)) decoder_1 (
    .out0(decoder_1_out0), .out1(decoder_1_out1), .out2(decoder_1_out2), .out3(decoder_1_out3), .sel(in_2));  // open: en
  and and_1 (and_1_out, decoder_1_out3, in_5[0]);
  and and_2 (and_2_out, decoder_1_out3, in_5[1]);
  and and_3 (and_3_out, decoder_1_out3, in_5[2]);
  and and_4 (and_4_out, in_1[0], decoder_1_out0);
  and and_5 (and_5_out, in_1[1], decoder_1_out0);
  and and_6 (and_6_out, in_1[2], decoder_1_out0);
  and and_7 (and_7_out, decoder_1_out1, in_3[0]);
  and and_8 (and_8_out, decoder_1_out1, in_3[1]);
  and and_9 (and_9_out, decoder_1_out1, in_3[2]);
  and and_10 (and_10_out, decoder_1_out2, in_4[0]);
  and and_11 (and_11_out, decoder_1_out2, in_4[1]);
  and and_12 (and_12_out, decoder_1_out2, in_4[2]);
  or or_1 (out_6, and_4_out, and_7_out, and_10_out, and_1_out);
  or or_2 (out_7, and_5_out, and_8_out, and_11_out, and_2_out);
  or or_3 (out_8, and_6_out, and_9_out, and_12_out, and_3_out);
endmodule
