// Logisim project one_s_complement_adder.circ as structural Verilog: 3 circuits, main circuit main
module main (
  input  [3:0] A,
  input  [3:0] B,
  output out_3,
  output [3:0] out_4
);

  wire comparator_1_eq, comparator_1_gt, comparator_1_lt, multiplexer_3_out, not_1_out, ones2signmag_1_sout,
       ones2signmag_2_sout, Op_Sel_out, or_1_out, SA_p1;
  wire [3:0] adder_1_out, multiplexer_1_out, multiplexer_2_out, multiplexer_4_out, ones2signmag_1_signmag,
       ones2signmag_2_signmag, subtractor_1_out;

  // DipSwitch #(.number(1)) SA: pin names not known; wires that end beside it: SA_p1
  // DipSwitch #(.number(1)) SB: pin names not known
  Ones2SignMag ones2signmag_1 (.S(SA_p1), .in_2(A), .Sout(ones2signmag_1_sout), .SignMag(ones2signmag_1_signmag));
  Ones2SignMag ones2signmag_2 (.in_2(B), .Sout(ones2signmag_2_sout), .SignMag(ones2signmag_2_signmag));  // open: S
  xor Op_Sel (Op_Sel_out, ones2signmag_1_sout, ones2signmag_2_sout);
  Adder #(.width(4)) adder_1 (
    .a(ones2signmag_1_signmag), .b(ones2signmag_2_signmag), .out(adder_1_out));  // open: cin, cout
  Comparator #(.mode("unsigned"), .width(4)) comparator_1 (
    .a(ones2signmag_1_signmag), .b(ones2signmag_2_signmag), .gt(comparator_1_gt), .eq(comparator_1_eq),
    .lt(comparator_1_lt));
  Multiplexer #(.width(4)) multiplexer_1 (
    .in0(ones2signmag_1_signmag), .in1(ones2signmag_2_signmag), .out(multiplexer_1_out), .sel(comparator_1_gt));
  Multiplexer #(.width(4)) multiplexer_2 (
    .in0(ones2signmag_1_signmag), .in1(ones2signmag_2_signmag), .out(multiplexer_2_out), .sel(comparator_1_lt));
  or or_1 (or_1_out, comparator_1_gt, comparator_1_eq);
  Subtractor #(.width(4)) subtractor_1 (
    .a(multiplexer_2_out), .b(multiplexer_1_out), .out(subtractor_1_out));  // open: bin, bout
  Multiplexer multiplexer_3 (
    .in0(ones2signmag_1_sout), .in1(ones2signmag_2_sout), .out(multiplexer_3_out), .sel(not_1_out));
  not not_1 (not_1_out, or_1_out);
  _7_Segment_Display u_7_segment_display_1 (.g(multiplexer_3_out));  // open: f, a, b, e, d, c, dp
  Multiplexer #(.width(4)) multiplexer_4 (
    .in0(adder_1_out), .in1(subtractor_1_out), .out(multiplexer_4_out), .sel(Op_Sel_out));
  Hex_Digit_Display hex_digit_display_1 (.value(multiplexer_4_out));  // open: dp
  Ones2SignMag ones2signmag_3 (.S(multiplexer_3_out), .in_2(multiplexer_4_out), .Sout(out_3), .SignMag(out_4));
endmodule

module adder1 (
  input  [3:0] A,
  input  [3:0] B
);

  wire comparator_1_eq, comparator_1_gt, comparator_1_lt, multiplexer_3_out, not_1_out, Op_Sel_out, or_1_out,
       SA_sw1, SB_p1;
  wire [3:0] adder_1_out, multiplexer_1_out, multiplexer_2_out, multiplexer_4_out, subtractor_1_out;

  DipSwitch #(.number(1)) SA (.sw1(SA_sw1));
  // DipSwitch #(.number(1)) SB: pin names not known; wires that end beside it: SB_p1
  xor Op_Sel (Op_Sel_out, SA_sw1, SB_p1);
  Adder #(.width(4)) adder_1 (.a(A), .b(B), .out(adder_1_out));  // open: cin, cout
  Comparator #(.mode("unsigned"), .width(4)) comparator_1 (
    .a(A), .b(B), .gt(comparator_1_gt), .eq(comparator_1_eq), .lt(comparator_1_lt));
  Multiplexer #(.width(4)) multiplexer_1 (.in0(A), .in1(B), .out(multiplexer_1_out), .sel(comparator_1_gt));
  Multiplexer #(.width(4)) multiplexer_2 (.in0(A), .in1(B), .out(multiplexer_2_out), .sel(comparator_1_lt));
  or or_1 (or_1_out, comparator_1_gt, comparator_1_eq);
  Subtractor #(.width(4)) subtractor_1 (
    .a(multiplexer_2_out), .b(multiplexer_1_out), .out(subtractor_1_out));  // open: bin, bout
  Multiplexer multiplexer_3 (.in0(SA_sw1), .in1(SB_p1), .out(multiplexer_3_out), .sel(not_1_out));
  not not_1 (not_1_out, or_1_out);
  Multiplexer #(.width(4)) multiplexer_4 (
    .in0(adder_1_out), .in1(subtractor_1_out), .out(multiplexer_4_out), .sel(Op_Sel_out));
  _7_Segment_Display u_7_segment_display_1 (.g(multiplexer_3_out));  // open: f, a, b, e, d, c, dp
  Hex_Digit_Display hex_digit_display_1 (.value(multiplexer_4_out));  // open: dp
endmodule

module Ones2SignMag (
  input  S,
  input  [3:0] in_2,
  output Sout,
  output [3:0] SignMag
);

  xor xor_1 (SignMag[0], S, in_2[0]);
  xor xor_2 (SignMag[1], S, in_2[1]);
  xor xor_3 (SignMag[2], S, in_2[2]);
  xor xor_4 (SignMag[3], S, in_2[3]);

  assign Sout = S;
endmodule
