// Logisim project overflow.circ as structural Verilog: 1 circuit, main circuit main
module main (
  input  [3:0] in_1,
  input  [3:0] in_2,
  output [3:0] out_3
);

  wire and_1_out, and_2_out, not_1_out, not_2_out, not_3_out, or_1_out;

  Adder #(.width(4)) adder_1 (.a(in_1), .b(in_2), .out(out_3));  // open: cin, cout
  not not_1 (not_1_out, in_2[3]);
  not not_2 (not_2_out, in_1[3]);
  not not_3 (not_3_out, out_3[3]);
  and and_1 (and_1_out, in_1[3], in_2[3], not_3_out);
  and and_2 (and_2_out, not_2_out, not_1_out, out_3[3]);
  or or_1 (or_1_out, and_1_out, and_2_out);
  LED led_1 (.in(or_1_out));
endmodule
