// Logisim project sign_and_magnitude_adder.circ as structural Verilog: 1 circuit, main circuit main
module main (
  input  [3:0] A,
  input  [3:0] B
);

  wire comparator_1_eq, comparator_1_gt, comparator_1_lt, multiplexer_3_out, Op_Sel_out, or_1_out, SA_sw1,
       SB_p1;
  wire [3:0] adder_1_out, multiplexer_1_out, multiplexer_2_out, multiplexer_4_out, subtractor_1_out;

  DipSwitch #(.number(1)) SA (.sw1(SA_sw1));
  // DipSwitch #(.number(1)) SB: pin names not known; wires that end beside it: SB_p1
  xor Op_Sel (Op_Sel_out, SA_sw1, SB_p1);
  Adder #(.width(4)) adder_1 (.a(A), .b(B), .out(adder_1_out));  // open: cin, cout
  Comparator #(.mode("unsigned"), .width(4)) comparator_1 (
    .a(A), .b(B), .gt(comparator_1_gt), .eq(comparator_1_eq), .lt(comparator_1_lt));
  Multiplexer #(.width(4)) multiplexer_1 (.in0(A), .in1(B), .out(multiplexer_1_out), .sel(comparator_1_gt));
  Multiplexer #(.width(4)) multiplexer_2 (.in0(A), .in1(B), .out(multiplexer_2_out), .sel(comparator_1_lt));
  or or_1 (or_1_out, comparator_1_gt, comparator_1_eq);
  Subtractor #(.width(4)) subtractor_1 (
    .a(multiplexer_1_out), .b(multiplexer_2_out), .out(subtractor_1_out));  // open: bin, bout
  Multiplexer multiplexer_3 (.in0(SA_sw1), .in1(SB_p1), .out(multiplexer_3_out), .sel(or_1_out));
  Multiplexer #(.width(4)) multiplexer_4 (
    .in0(adder_1_out), .in1(subtractor_1_out), .out(multiplexer_4_out), .sel(Op_Sel_out));
  _7_Segment_Display u_7_segment_display_1 (.g(multiplexer_3_out));  // open: f, a, b, e, d, c, dp
  Hex_Digit_Display hex_digit_display_1 (.value(multiplexer_4_out));  // open: dp
endmodule
