// Logisim project RAM1.circ as structural Verilog: 1 circuit, main circuit main
module main (
  input  [7:0] Data,
  input  [1:0] addr,
  input  EN
);

  wire and_1_out, and_2_out, and_3_out, and_4_out, clock_1_out, decoder_1_out0, decoder_1_out1,
       decoder_1_out2, decoder_1_out3;

  Clock clock_1 (.out(clock_1_out));
  Decoder #(.select(2)) decoder_1 (
    .out0(decoder_1_out0), .out1(decoder_1_out1), .out2(decoder_1_out2), .out3(decoder_1_out3), .sel(addr));  // open: en
  Register r0 (.D(Data), .en(and_1_out), .clk(clock_1_out));  // open: Q, clr
  and and_1 (and_1_out, decoder_1_out0, EN);
  Register r2 (.D(Data), .en(and_2_out), .clk(clock_1_out));  // open: Q, clr
  and and_2 (and_2_out, decoder_1_out2, EN);
  Register r1 (.D(Data), .en(and_3_out), .clk(clock_1_out));  // open: Q, clr
  and and_3 (and_3_out, decoder_1_out1, EN);
  Register r3 (.D(Data), .en(and_4_out), .clk(clock_1_out));  // open: Q, clr
  and and_4 (and_4_out, decoder_1_out3, EN);
endmodule
