// Logisim project ROM(F5_1_1).circ as structural Verilog: 1 circuit, main circuit main
module main (
  output [7:0] out_1
);

  wire clock_1_out;
  wire [2:0] adder_1_out, PC_q;

  Clock clock_1 (.out(clock_1_out));
  Register #(.width(3)) PC (.D(adder_1_out), .en(1'b1), .clk(clock_1_out), .Q(PC_q));  // open: clr
  Multiplexer #(.select(3), .width(8)) multiplexer_1 (
    .in0(8'h8a), .in1(8'h90), .in2(8'ha0), .in3(8'hb1), .in4(8'hb1), .in5(8'ha0), .in6(8'h90), .in7(8'h8a),
    .out(out_1), .sel(PC_q));
  Adder #(.width(3)) adder_1 (.a(PC_q), .b(3'b001), .out(adder_1_out));  // open: cin, cout
endmodule
