// Logisim project sCPU_4.circ as structural Verilog: 2 circuits, main circuit main
module main (
  output [7:0] r0,
  output [7:0] r1,
  output [7:0] r2,
  output [7:0] r3
);

  wire and_1_out, clock_1_out, comparator_1_eq, decoder_1_out0, decoder_1_out1, decoder_1_out2,
       decoder_1_out3, not_1_out, or_1_out, Reset_out;
  wire [3:0] adder_1_out, multiplexer_1_out, multiplexer_2_out_2, PC_q;
  wire [7:0] adder_2_out, bit_extender_1_out, multiplexer_2_out, multiplexer_3_out, multiplexer_4_out,
       ram1_1_rdata1, ram1_1_rdata2;

  and and_1 (and_1_out, decoder_1_out3, not_1_out);
  Register #(.width(4)) PC (.D(multiplexer_1_out), .en(1'b1), .clk(clock_1_out), .Q(PC_q), .clr(Reset_out));
  Multiplexer #(.width(4)) multiplexer_1 (
    .in0(adder_1_out), .in1(multiplexer_2_out_2), .out(multiplexer_1_out), .sel(and_1_out));
  Button Reset (.out(Reset_out));
  Multiplexer #(.select(4), .width(8)) multiplexer_2 (
    .in0(8'h8a), .in1(8'h90), .in2(8'ha0), .in3(8'hb1), .in4(8'h17), .in5(8'h29), .in6(8'hd1), .in7(8'h48),
    .in8(8'hb8), .in9(8'hc0), .out({multiplexer_2_out[7:6], multiplexer_2_out_2, multiplexer_2_out[1:0]}),
    .sel(PC_q));  // open: in10, in11, in12, in13, in14, in15
  // Probe on multiplexer_2_out[7:6]
  Adder #(.width(4)) adder_1 (.a(PC_q), .b(4'b0001), .out(adder_1_out));  // open: cin, cout
  Clock clock_1 (.out(clock_1_out));
  Comparator #(.mode("unsigned")) comparator_1 (.a(r0), .b(ram1_1_rdata1), .eq(comparator_1_eq));  // open: gt, lt
  Decoder #(.select(2)) decoder_1 (
    .out0(decoder_1_out0), .out1(decoder_1_out1), .out2(decoder_1_out2), .out3(decoder_1_out3),
    .sel(multiplexer_2_out[7:6]));  // open: en
  not not_1 (not_1_out, comparator_1_eq);
  or or_1 (or_1_out, decoder_1_out0, 1'b0, decoder_1_out2);
  Multiplexer #(.width(8)) multiplexer_3 (
    .in0({8{1'b0}}), .in1(ram1_1_rdata2), .out(multiplexer_3_out), .sel(decoder_1_out1));
  assign bit_extender_1_out = {{4{1'b0}}, {multiplexer_2_out_2[1:0], multiplexer_2_out[1:0]}};  // Bit_Extender bit_extender_1
  RAM1 ram1_1 (
    .waddr(multiplexer_2_out_2[3:2]), .wdata(multiplexer_4_out), .EN(or_1_out),
    .raddr1(multiplexer_2_out[1:0]), .raddr2(multiplexer_2_out_2[1:0]), .clk(clock_1_out),
    .rdata1(ram1_1_rdata1), .rdata2(ram1_1_rdata2), .rr0(r0), .rr1(r1), .rr2(r2), .rr3(r3));
  Multiplexer #(.select(2), .width(8)) multiplexer_4 (
    .in0(adder_2_out), .in2(bit_extender_1_out), .out(multiplexer_4_out), .sel(multiplexer_2_out[7:6]));  // open: in1, in3
  Adder adder_2 (.a(ram1_1_rdata1), .b(ram1_1_rdata2), .out(adder_2_out));  // open: cin, cout
  Hex_Digit_Display hex_digit_display_1 (.value(multiplexer_3_out[7:4]));  // open: dp
  Hex_Digit_Display hex_digit_display_2 (.value(multiplexer_3_out[3:0]));  // open: dp
endmodule

module RAM1 (
  input  [1:0] waddr,
  input  [7:0] wdata,
  input  EN,
  input  [1:0] raddr1,
  input  [1:0] raddr2,
  input  clk,
  output [7:0] rdata1,
  output [7:0] rdata2,
  output [7:0] rr0,
  output [7:0] rr1,
  output [7:0] rr2,
  output [7:0] rr3
);

  wire and_1_out, and_2_out, and_3_out, and_4_out, decoder_1_out0, decoder_1_out1, decoder_1_out2,
       decoder_1_out3;

  Decoder #(.select(2)) decoder_1 (
    .out0(decoder_1_out0), .out1(decoder_1_out1), .out2(decoder_1_out2), .out3(decoder_1_out3), .sel(waddr));  // open: en
  Register r0 (.D(wdata), .en(and_1_out), .clk(clk), .Q(rr0));  // open: clr
  and and_1 (and_1_out, decoder_1_out0, EN);
  Register r2 (.D(wdata), .en(and_2_out), .clk(clk), .Q(rr2));  // open: clr
  and and_2 (and_2_out, decoder_1_out2, EN);
  Register r1 (.D(wdata), .en(and_3_out), .clk(clk), .Q(rr1));  // open: clr
  and and_3 (and_3_out, decoder_1_out1, EN);
  Register r3 (.D(wdata), .en(and_4_out), .clk(clk), .Q(rr3));  // open: clr
  and and_4 (and_4_out, decoder_1_out3, EN);
  Multiplexer #(.select(2), .width(8)) multiplexer_1 (
    .in0(rr0), .in1(rr1), .in2(rr2), .in3(rr3), .out(rdata1), .sel(raddr1));
  Multiplexer #(.select(2), .width(8)) multiplexer_2 (
    .in0(rr0), .in1(rr1), .in2(rr2), .in3(rr3), .out(rdata2), .sel(raddr2));
endmodule
