// Logisim project sCPU_li.circ as structural Verilog
module main (
  input  EN
);

  wire and_1_out, and_2_out, and_3_out, and_4_out, clock_1_out, decoder_1_out0, decoder_1_out1,
       decoder_1_out2, decoder_1_out3;
  wire [1:0] adder_1_out, PC_q;
  wire [7:0] bit_extender_1_out, multiplexer_1_out;

  Register #(.width(2)) PC (.D(adder_1_out), .en(1'b1), .clk(clock_1_out), .Q(PC_q));  // open: clr
  // Probe on multiplexer_1_out
  Multiplexer #(.select(2), .width(8)) multiplexer_1 (
    .in0(8'h8a), .in1(8'h90), .in2(8'ha0), .in3(8'hb1), .out(multiplexer_1_out), .sel(PC_q));
  Adder #(.width(2)) adder_1 (.a(PC_q), .b(2'b01), .out(adder_1_out));  // open: cin, cout
  // NoConnect on multiplexer_1_out[7:6]
  assign bit_extender_1_out = {{4{1'b0}}, multiplexer_1_out[3:0]};  // Bit_Extender bit_extender_1
  Clock clock_1 (.out(clock_1_out));
  Decoder #(.select(2)) decoder_1 (
    .out0(decoder_1_out0), .out1(decoder_1_out1), .out2(decoder_1_out2), .out3(decoder_1_out3),
    .sel(multiplexer_1_out[5:4]));  // open: en
  Register r0 (.D(bit_extender_1_out), .en(and_1_out), .clk(clock_1_out));  // open: Q, clr
  and and_1 (and_1_out, decoder_1_out0, EN);
  Register r2 (.D(bit_extender_1_out), .en(and_2_out), .clk(clock_1_out));  // open: Q, clr
  and and_2 (and_2_out, decoder_1_out2, EN);
  Register r1 (.D(bit_extender_1_out), .en(and_3_out), .clk(clock_1_out));  // open: Q, clr
  and and_3 (and_3_out, decoder_1_out1, EN);
  Register r3 (.D(bit_extender_1_out), .en(and_4_out), .clk(clock_1_out));  // open: Q, clr
  and and_4 (and_4_out, decoder_1_out3, EN);
endmodule
