// Logisim project minirv_3_RGBVideo.circ as structural Verilog: 10 circuits, main circuit main
module main (
);

  wire and_1_out, and_2_out, and_3_out, button_1_out, clock_1_out, comparator_1_eq, comparator_1_gt,
       comparator_2_lt, decoder_1_out0, decoder_1_out1, decoder_1_out2, decoder_1_out3, is_addi_1_true,
       is_jalr_1_true, is_lbu_1_true, is_lui_1_true, is_lw_1_true, is_sb_1_true, is_sw_1_true, not_1_out,
       not_2_out, or_1_out, or_2_out, or_5_out, or_6_out, or_7_out, or_8_out, or_9_out, undriven;
  wire [1:0] adder_3_out, or_3_out;
  wire [3:0] rom_1_data_2;
  wire [4:4] rom_1_data_3;
  wire [6:0] rom_1_data_4;
  wire [7:0] minirv_gpr_1_rdata2_3, multiplexer_7_out, ram_1_dout, ram_1_dout_2, ram_1_dout_3, ram_1_dout_4;
  wire [11:0] multiplexer_3_out;
  wire [19:0] adder_3_out_2, PC_q_2;
  wire [23:8] minirv_gpr_1_rdata2;
  wire [31:0] adder_1_out, bit_extender_1_out, bit_extender_2_out, minirv_gpr_1_rdata1, multiplexer_1_out,
       multiplexer_2_out, multiplexer_4_out, multiplexer_5_out, multiplexer_6_out, PC_q;
  wire [31:12] rom_1_data;
  wire [31:22] adder_3_out_3;
  wire [31:24] minirv_gpr_1_rdata2_2;
  wire [63:0] adder_2_out, Cycle_Cnt_q;

  Clock clock_1 (.out(clock_1_out));
  Multiplexer #(.width(32)) multiplexer_1 (
    .in0(adder_1_out), .in1({adder_3_out_3, adder_3_out_2, adder_3_out}), .out(multiplexer_1_out),
    .sel(is_jalr_1_true));
  // Probe on {adder_3_out_3, adder_3_out_2, adder_3_out}
  Register #(.width(32)) PC (
    .D(multiplexer_1_out), .en(1'b1), .clk(clock_1_out), .Q({PC_q[31:22], PC_q_2, PC_q[1:0]}),
    .clr(button_1_out));
  Button button_1 (.out(button_1_out));
  Adder #(.width(32)) adder_1 (.a({PC_q[31:22], PC_q_2, PC_q[1:0]}), .b(32'h4), .out(adder_1_out));  // open: cin, cout
  Register #(.width(64)) Cycle_Cnt (.D(adder_2_out), .en(1'b1), .clk(clock_1_out), .Q(Cycle_Cnt_q), .clr(button_1_out));
  Adder #(.width(64)) adder_2 (.a(Cycle_Cnt_q), .b(64'h1), .out(adder_2_out));  // open: cin, cout
  ROM #(.addrWidth(20), .dataWidth(32)) rom_1 (
    .addr(PC_q_2), .data({rom_1_data, rom_1_data_3[4], rom_1_data_2, rom_1_data_4}));
  Multiplexer #(.select(2), .width(32)) multiplexer_2 (
    .in0({adder_3_out_3, adder_3_out_2, adder_3_out}), .in1(adder_1_out), .in2({rom_1_data, {12{1'b0}}}),
    .in3(multiplexer_6_out), .out(multiplexer_2_out), .sel(or_3_out));
  Multiplexer #(.width(12)) multiplexer_3 (
    .in0(rom_1_data[31:20]), .in1({rom_1_data[31:25], rom_1_data_3[4], rom_1_data_2}),
    .out(multiplexer_3_out), .sel(or_2_out));
  minirv_GPR minirv_gpr_1 (
    .clk(clock_1_out), .wdata(multiplexer_2_out), .waddr(rom_1_data_2), .wEN(not_1_out),
    .rs1(rom_1_data[18:15]), .RST(button_1_out), .rs2(rom_1_data[23:20]), .rdata1(minirv_gpr_1_rdata1),
    .rdata2({minirv_gpr_1_rdata2_2, minirv_gpr_1_rdata2, minirv_gpr_1_rdata2_3}));
  is_addi is_addi_1 (.OP(rom_1_data_4), .F3(rom_1_data[14:12]), .true(is_addi_1_true));
  is_jalr is_jalr_1 (.OP(rom_1_data_4), .F3(rom_1_data[14:12]), .true(is_jalr_1_true));
  is_add is_add_1 (.OP(rom_1_data_4), .F3(rom_1_data[14:12]), .F7(rom_1_data[31:25]));  // open: true
  is_lui is_lui_1 (.OP(rom_1_data_4), .true(is_lui_1_true));
  is_lw is_lw_1 (.OP(rom_1_data_4), .F3(rom_1_data[14:12]), .true(is_lw_1_true));
  is_sw is_sw_1 (.OP(rom_1_data_4), .F3(rom_1_data[14:12]), .true(is_sw_1_true));
  is_lbu is_lbu_1 (.OP(rom_1_data_4), .F3(rom_1_data[14:12]), .true(is_lbu_1_true));
  is_sb is_sb_1 (.OP(rom_1_data_4), .F3(rom_1_data[14:12]), .true(is_sb_1_true));
  // Probe on undriven
  Multiplexer #(.width(32)) multiplexer_4 (
    .in0({minirv_gpr_1_rdata2_2, minirv_gpr_1_rdata2, minirv_gpr_1_rdata2_3}), .in1(bit_extender_1_out),
    .out(multiplexer_4_out), .sel(or_1_out));
  assign bit_extender_1_out = {{20{multiplexer_3_out[11]}}, multiplexer_3_out};  // Bit_Extender bit_extender_1
  not not_1 (not_1_out, or_2_out);
  Adder #(.width(32)) adder_3 (
    .a(minirv_gpr_1_rdata1), .b(multiplexer_4_out), .out({adder_3_out_3, adder_3_out_2, adder_3_out}));  // open: cin, cout
  or or_1 (or_1_out, is_addi_1_true, is_lbu_1_true, is_sb_1_true, is_sw_1_true, is_lw_1_true);
  or or_2 (or_2_out, is_sw_1_true, is_sb_1_true);
  or or_3 (or_3_out[0], is_jalr_1_true, is_lbu_1_true, is_lw_1_true);
  or or_4 (or_3_out[1], is_lw_1_true, is_lbu_1_true, is_lui_1_true);
  Decoder #(.select(2)) decoder_1 (
    .out0(decoder_1_out0), .out1(decoder_1_out1), .out2(decoder_1_out2), .out3(decoder_1_out3),
    .sel(adder_3_out));  // open: en
  not not_2 (not_2_out, and_2_out);
  Comparator #(.mode("unsigned"), .width(32)) comparator_1 (
    .a({adder_3_out_3, adder_3_out_2, adder_3_out}), .b(32'h20000000), .gt(comparator_1_gt),
    .eq(comparator_1_eq));  // open: lt
  Comparator #(.mode("unsigned"), .width(32)) comparator_2 (
    .a({adder_3_out_3, adder_3_out_2, adder_3_out}), .b(32'h20040000), .lt(comparator_2_lt));  // open: gt, eq
  RAM #(.addrWidth(20), .asyncread("true"), .byteenables("byteEnables"), .dataWidth(32), .\type ("nonvolatile")) ram_1 (
    .addr(adder_3_out_2), .we(and_1_out), .oe(1'b1), .clk(clock_1_out), .din(multiplexer_5_out),
    .dout({ram_1_dout_4, ram_1_dout_3, ram_1_dout_2, ram_1_dout}), .be3(or_8_out), .be2(or_7_out),
    .be1(or_6_out), .be0(or_5_out));
  and and_1 (and_1_out, or_2_out, not_2_out);
  Multiplexer #(.width(32)) multiplexer_5 (
    .in0({minirv_gpr_1_rdata2_2, minirv_gpr_1_rdata2, minirv_gpr_1_rdata2_3}),
    .in1({minirv_gpr_1_rdata2_3, minirv_gpr_1_rdata2_3, minirv_gpr_1_rdata2_3, minirv_gpr_1_rdata2_3}),
    .out(multiplexer_5_out), .sel(is_sb_1_true));
  or or_5 (or_5_out, is_sw_1_true, decoder_1_out0);
  or or_6 (or_6_out, is_sw_1_true, decoder_1_out1);
  or or_7 (or_7_out, decoder_1_out2, is_sw_1_true);
  or or_8 (or_8_out, decoder_1_out3, is_sw_1_true);
  or or_9 (or_9_out, comparator_1_gt, comparator_1_eq);
  and and_2 (and_2_out, or_9_out, comparator_2_lt);
  and and_3 (and_3_out, and_2_out, is_sw_1_true);
  Multiplexer #(.width(32)) multiplexer_6 (
    .in0({ram_1_dout_4, ram_1_dout_3, ram_1_dout_2, ram_1_dout}), .in1(bit_extender_2_out),
    .out(multiplexer_6_out), .sel(is_lbu_1_true));
  assign bit_extender_2_out = {{24{1'b0}}, multiplexer_7_out};  // Bit_Extender bit_extender_2
  Multiplexer #(.select(2), .width(8)) multiplexer_7 (
    .in0(ram_1_dout), .in1(ram_1_dout_2), .in2(ram_1_dout_3), .in3(ram_1_dout_4), .out(multiplexer_7_out),
    .sel(adder_3_out));
  // RGB_Video #(.cursor("No Cursor"), .height(256), .scale(1), .width(256)) rgb_video_1: pin names not known; wires that end beside it: button_1_out, clock_1_out, and_3_out, adder_3_out_2[7:0], adder_3_out_2[15:8], {minirv_gpr_1_rdata2, minirv_gpr_1_rdata2_3}

  // Notes on the sheet:
  //   contents of rom_1 (hex, n*v repeats v):
  //   413 93137 10113 10b7 dbc08093 80e7 fe012823 fea10923 fea12423 fe914203 fe4109a3 ff012783 f787b3
  //   f787b3 4b6b7 f0068693 fdc10113 d787b3 10000713 f12423 10593 100793 b00513 2112023 12023 12223 e12623
  //   e12823 f10a23 10b7 a8408093 80e7 2012083 2410113 8067 ff410113 112423 10b7 a7c08093 80e7 513 1800093
  //   80e7 812083 513 c10113 8067 852583 feb12823 fe812e23 3437 a0840413 ff014183 3401b3 1c183 ff114203
  //   440233 24203 4181b3 ff214203 440233 24203 4181b3 ff314203 440233 24203 4181b3 3237 a0020213 320233
  //   24203 ffc12403 420233 420233 410233 11b7 85c18193 fe312823 14800193 fe312623 fec22203 20067 1052703
  //   52683 452783 fe810113 e12423 112a23 fed12823 fef12623 13737 c0070713 fe012223 ff314203 fe4102a3
  //   fef14203 fe410223 fe412203 470233 24203 fe4105a3 ff214203 fe4102a3 fee14203 fe410223 fe412203 470233
  //   24203 fe410523 ff114203 fe4102a3 fed14203 fe410223 fe412203 470233 24203 fe4104a3 ff014203 fe4102a3
  //   fec14203 fe410223 fe412203 470233 24203 fe410423 fe812703 c52603 fee12823 fe812e23 3437 a0840413
  //   ff014183 3401b3 1c183 ff114203 440233 24203 4181b3 ff214203 440233 24203 4181b3 ff314203 440233
  //   24203 4181b3 3237 a0020213 320233 24203 ffc12403 420233 420233 410233 66800193 fe312823 28000193
  //   fe312623 fec22203 20067 c68733 10000513 fe812e23 fe912c23 fee12823 50413 ff012483 fe812423 feb14183
  //   3181b3 fe312423 fe914183 3181b3 fe912423 feb14203 420233 fe412423 fe914203 4181b3 3181b3 fe312a23
  //   fe912423 33237 b0020213 feb14183 4181b3 1c183 fe3103a3 fea14183 4181b3 1c183 fe310323 fe914183
  //   4181b3 1c183 fe3102a3 fe814183 4181b3 1c183 fe310223 ff412183 fe412203 440233 120213 fe412423
  //   feb14203 420233 fe412423 fe914203 4181b3 3237 b0820213 320233 ff812483 ffc12403 24203 420233 420233
  //   410233 11b7 86018193 fe312823 38800193 fe312623 fec22203 20067 812703 10000513 812823 e78733
  //   fe812e23 fe912c23 fee12823 50413 ff012483 fe812423 feb14183 3181b3 fe312423 fe914183 3181b3 fe912423
  //   feb14203 420233 fe412423 fe914203 4181b3 3181b3 fe312a23 fe912423 33237 b0020213 feb14183 4181b3
  //   1c183 fe3103a3 fea14183 4181b3 1c183 fe310323 fe914183 4181b3 1c183 fe3102a3 fe814183 4181b3 1c183
  //   fe310223 ff412183 fe412203 440233 120213 fe412423 feb14203 420233 fe412423 fe914203 4181b3 3237
  //   b0820213 320233 ff812483 ffc12403 24203 420233 420233 410233 11b7 86418193 fe312823 49800193
  //   fe312623 fec22203 20067 8*f787b3 d787b3 f787b3 f787b3 20000437 f40433 812783 c60633 c60633 fef12423
  //   feb14183 3181b3 fe312423 fe914183 fff78213 fe412423 feb14203 420233 fe412423 fe914203 4181b3 3237
  //   b1820213 418233 24203 420233 420233 410233 65800193 fe312823 53c00193 fe312623 fec22203 20067 912623
  //   493 40513 c12223 b12023 10b7 de008093 80e7 12583 412603 812783 148493 40040413 c585b3 fef12823
  //   fe912623 fe812e23 fe912c23 4b437 d0040413 ff014183 340233 100193 320023 fec14183 3401b3 18023 24183
  //   ff114483 940233 100493 920023 fed14483 9404b3 48023 24483 9181b3 ff214483 940233 100493 920023
  //   fee14483 9404b3 48023 24483 9181b3 ff314483 940233 100493 920023 fef14483 9404b3 48023 24483 9181b3
  //   3237 a0020213 320233 24203 ff812483 ffc12403 420233 420233 410233 65400193 fe312823 54400193
  //   fe312623 fec22203 20067 c12483 1012403 1412083 1810113 8067 10000713 fec12823 fee12623 fe812e23
  //   fe912c23 4b437 d0040413 ff014183 340233 100193 320023 fec14183 3401b3 18023 24183 ff114483 940233
  //   100493 920023 fed14483 9404b3 48023 24483 9181b3 ff214483 940233 100493 920023 fee14483 9404b3 48023
  //   24483 9181b3 ff314483 940233 100493 920023 fef14483 9404b3 48023 24483 9181b3 3237 a0020213 320233
  //   24203 ff812483 ffc12403 420233 420233 410233 74c00193 fe312823 28000193 fe312623 fec22203 20067
  //   812703 fee12823 fec12623 fe812e23 fe912c23 4b437 d0040413 ff014183 340233 100193 320023 fec14183
  //   3401b3 18023 24183 ff114483 940233 100493 920023 fed14483 9404b3 48023 24483 9181b3 ff214483 940233
  //   100493 920023 fee14483 9404b3 48023 24483 9181b3 ff314483 940233 100493 920023 fef14483 9404b3 48023
  //   24483 9181b3 3237 a0020213 320233 24203 ff812483 ffc12403 420233 420233 410233 11b7 83418193
  //   fe312823 38800193 fe312623 fec22203 20067 1412083 40637 20000537 1810113 1237 de020213 20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
endmodule

module minirv_GPR (
  input  clk,
  input  [31:0] wdata,
  input  [3:0] waddr,
  input  wEN,
  input  [3:0] rs1,
  input  RST,
  input  [3:0] rs2,
  output [31:0] rdata1,
  output [31:0] rdata2
);

  wire decoder_1_out1, decoder_1_out2, decoder_1_out3, decoder_1_out4, decoder_1_out5, decoder_1_out6,
       decoder_1_out7, decoder_1_out8, decoder_1_out9, decoder_1_out10, decoder_1_out11, decoder_1_out12,
       decoder_1_out13, decoder_1_out14, decoder_1_out15;
  wire [31:0] register_1_q, register_2_q, register_3_q, register_4_q, register_5_q, register_6_q,
       register_7_q, register_8_q, register_9_q, register_10_q, register_11_q, register_12_q, register_13_q,
       register_14_q, register_15_q, register_16_q;

  Decoder #(.select(4)) decoder_1 (
    .out1(decoder_1_out1), .out2(decoder_1_out2), .out3(decoder_1_out3), .out4(decoder_1_out4),
    .out5(decoder_1_out5), .out6(decoder_1_out6), .out7(decoder_1_out7), .out8(decoder_1_out8),
    .out9(decoder_1_out9), .out10(decoder_1_out10), .out11(decoder_1_out11), .out12(decoder_1_out12),
    .out13(decoder_1_out13), .out14(decoder_1_out14), .out15(decoder_1_out15), .sel(waddr), .en(wEN));  // open: out0
  Register #(.width(32)) register_1 (.D(wdata), .en(1'b0), .clk(clk), .Q(register_1_q), .clr(RST));
  Register #(.width(32)) register_2 (.D(wdata), .en(decoder_1_out8), .clk(clk), .Q(register_2_q), .clr(RST));
  Register #(.width(32)) register_3 (.D(wdata), .en(decoder_1_out1), .clk(clk), .Q(register_3_q), .clr(RST));
  Register #(.width(32)) register_4 (.D(wdata), .en(decoder_1_out9), .clk(clk), .Q(register_4_q), .clr(RST));
  Register #(.width(32)) register_5 (.D(wdata), .en(decoder_1_out2), .clk(clk), .Q(register_5_q), .clr(RST));
  Register #(.width(32)) register_6 (.D(wdata), .en(decoder_1_out10), .clk(clk), .Q(register_6_q), .clr(RST));
  Register #(.width(32)) register_7 (.D(wdata), .en(decoder_1_out3), .clk(clk), .Q(register_7_q), .clr(RST));
  Register #(.width(32)) register_8 (.D(wdata), .en(decoder_1_out11), .clk(clk), .Q(register_8_q), .clr(RST));
  Register #(.width(32)) register_9 (.D(wdata), .en(decoder_1_out4), .clk(clk), .Q(register_9_q), .clr(RST));
  Register #(.width(32)) register_10 (.D(wdata), .en(decoder_1_out12), .clk(clk), .Q(register_10_q), .clr(RST));
  Register #(.width(32)) register_11 (.D(wdata), .en(decoder_1_out5), .clk(clk), .Q(register_11_q), .clr(RST));
  Register #(.width(32)) register_12 (.D(wdata), .en(decoder_1_out13), .clk(clk), .Q(register_12_q), .clr(RST));
  Register #(.width(32)) register_13 (.D(wdata), .en(decoder_1_out6), .clk(clk), .Q(register_13_q), .clr(RST));
  Register #(.width(32)) register_14 (.D(wdata), .en(decoder_1_out14), .clk(clk), .Q(register_14_q), .clr(RST));
  Register #(.width(32)) register_15 (.D(wdata), .en(decoder_1_out7), .clk(clk), .Q(register_15_q), .clr(RST));
  Register #(.width(32)) register_16 (.D(wdata), .en(decoder_1_out15), .clk(clk), .Q(register_16_q), .clr(RST));
  Multiplexer #(.select(4), .width(32)) multiplexer_1 (
    .in0(register_1_q), .in1(register_3_q), .in2(register_5_q), .in3(register_7_q), .in4(register_9_q),
    .in5(register_11_q), .in6(register_13_q), .in7(register_15_q), .in8(register_2_q), .in9(register_4_q),
    .in10(register_6_q), .in11(register_8_q), .in12(register_10_q), .in13(register_12_q),
    .in14(register_14_q), .in15(register_16_q), .out(rdata1), .sel(rs1));
  Multiplexer #(.select(4), .width(32)) multiplexer_2 (
    .in0(register_1_q), .in1(register_3_q), .in2(register_5_q), .in3(register_7_q), .in4(register_9_q),
    .in5(register_11_q), .in6(register_13_q), .in7(register_15_q), .in8(register_2_q), .in9(register_4_q),
    .in10(register_6_q), .in11(register_8_q), .in12(register_10_q), .in13(register_12_q),
    .in14(register_14_q), .in15(register_16_q), .out(rdata2), .sel(rs2));
endmodule

module is_addi (
  input  [6:0] OP,
  input  [2:0] F3,
  output true
);

  wire comparator_1_eq, comparator_2_eq;

  Comparator #(.mode("unsigned"), .width(7)) comparator_1 (
    .a(OP), .b(7'b0010011), .eq(comparator_1_eq));  // open: gt, lt
  Comparator #(.mode("unsigned"), .width(3)) comparator_2 (.a(F3), .b(3'b000), .eq(comparator_2_eq));  // open: gt, lt
  and and_1 (true, comparator_1_eq, comparator_2_eq);
endmodule

module is_jalr (
  input  [6:0] OP,
  input  [2:0] F3,
  output true
);

  wire comparator_1_eq, comparator_2_eq;

  Comparator #(.mode("unsigned"), .width(7)) comparator_1 (
    .a(OP), .b(7'b1100111), .eq(comparator_1_eq));  // open: gt, lt
  Comparator #(.mode("unsigned"), .width(3)) comparator_2 (.a(F3), .b(3'b000), .eq(comparator_2_eq));  // open: gt, lt
  and and_1 (true, comparator_1_eq, comparator_2_eq);
endmodule

module is_add (
  input  [6:0] OP,
  input  [2:0] F3,
  input  [6:0] F7,
  output true
);

  wire comparator_1_eq, comparator_2_eq, comparator_3_eq;

  Comparator #(.mode("unsigned"), .width(7)) comparator_1 (
    .a(OP), .b(7'b0110011), .eq(comparator_1_eq));  // open: gt, lt
  Comparator #(.mode("unsigned"), .width(3)) comparator_2 (.a(F3), .b(3'b000), .eq(comparator_2_eq));  // open: gt, lt
  Comparator #(.mode("unsigned"), .width(7)) comparator_3 (
    .a(F7), .b({7{1'b0}}), .eq(comparator_3_eq));  // open: gt, lt
  and and_1 (true, comparator_1_eq, comparator_2_eq, comparator_3_eq);
endmodule

module is_lui (
  input  [6:0] OP,
  output true
);

  Comparator #(.mode("unsigned"), .width(7)) comparator_1 (.a(OP), .b(7'b0110111), .eq(true));  // open: gt, lt
endmodule

module is_lw (
  input  [6:0] OP,
  input  [2:0] F3,
  output true
);

  wire comparator_1_eq, comparator_2_eq;

  Comparator #(.mode("unsigned"), .width(7)) comparator_1 (
    .a(OP), .b(7'b0000011), .eq(comparator_1_eq));  // open: gt, lt
  Comparator #(.mode("unsigned"), .width(3)) comparator_2 (.a(F3), .b(3'b010), .eq(comparator_2_eq));  // open: gt, lt
  and and_1 (true, comparator_1_eq, comparator_2_eq);
endmodule

module is_sw (
  input  [6:0] OP,
  input  [2:0] F3,
  output true
);

  wire comparator_1_eq, comparator_2_eq;

  Comparator #(.mode("unsigned"), .width(7)) comparator_1 (
    .a(OP), .b(7'b0100011), .eq(comparator_1_eq));  // open: gt, lt
  Comparator #(.mode("unsigned"), .width(3)) comparator_2 (.a(F3), .b(3'b010), .eq(comparator_2_eq));  // open: gt, lt
  and and_1 (true, comparator_1_eq, comparator_2_eq);
endmodule

module is_lbu (
  input  [6:0] OP,
  input  [2:0] F3,
  output true
);

  wire comparator_1_eq, comparator_2_eq;

  Comparator #(.mode("unsigned"), .width(7)) comparator_1 (
    .a(OP), .b(7'b0000011), .eq(comparator_1_eq));  // open: gt, lt
  Comparator #(.mode("unsigned"), .width(3)) comparator_2 (.a(F3), .b(3'b100), .eq(comparator_2_eq));  // open: gt, lt
  and and_1 (true, comparator_1_eq, comparator_2_eq);
endmodule

module is_sb (
  input  [6:0] OP,
  input  [2:0] F3,
  output true
);

  wire comparator_1_eq, comparator_2_eq;

  Comparator #(.mode("unsigned"), .width(7)) comparator_1 (
    .a(OP), .b(7'b0100011), .eq(comparator_1_eq));  // open: gt, lt
  Comparator #(.mode("unsigned"), .width(3)) comparator_2 (.a(F3), .b(3'b000), .eq(comparator_2_eq));  // open: gt, lt
  and and_1 (true, comparator_1_eq, comparator_2_eq);
endmodule
