// Logisim project minirv_3_c.circ as structural Verilog: 10 circuits, main circuit main
module main (
);

  wire button_1_out, clock_1_out, decoder_1_out0, decoder_1_out1, decoder_1_out2, decoder_1_out3,
       is_addi_1_true, is_jalr_1_true, is_lbu_1_true, is_lui_1_true, is_lw_1_true, is_sb_1_true,
       is_sw_1_true, not_1_out, or_1_out, or_2_out, or_5_out, or_6_out, or_7_out, or_8_out, undriven;
  wire [1:0] adder_3_out, or_3_out;
  wire [3:0] rom_1_data_2;
  wire [4:4] rom_1_data_3;
  wire [6:0] rom_1_data_4;
  wire [7:0] minirv_gpr_1_rdata2_2, multiplexer_7_out, ram_1_dout, ram_1_dout_2, ram_1_dout_3, ram_1_dout_4;
  wire [11:0] multiplexer_3_out;
  wire [19:0] adder_3_out_2, PC_q_2;
  wire [31:0] adder_1_out, bit_extender_1_out, bit_extender_2_out, minirv_gpr_1_rdata1, multiplexer_1_out,
       multiplexer_2_out, multiplexer_4_out, multiplexer_5_out, multiplexer_6_out, PC_q;
  wire [31:8] minirv_gpr_1_rdata2;
  wire [31:12] rom_1_data;
  wire [31:22] adder_3_out_3;
  wire [63:0] adder_2_out, Cycle_Cnt_q;

  Clock clock_1 (.out(clock_1_out));
  Multiplexer #(.width(32)) multiplexer_1 (
    .in0(adder_1_out), .in1({adder_3_out_3, adder_3_out_2, adder_3_out}), .out(multiplexer_1_out),
    .sel(is_jalr_1_true));
  // Probe on {adder_3_out_3, adder_3_out_2, adder_3_out}
  Register #(.width(32)) PC (
    .D(multiplexer_1_out), .en(1'b1), .clk(clock_1_out), .Q({PC_q[31:22], PC_q_2, PC_q[1:0]}),
    .clr(button_1_out));
  Button button_1 (.out(button_1_out));
  Adder #(.width(32)) adder_1 (.a({PC_q[31:22], PC_q_2, PC_q[1:0]}), .b(32'h4), .out(adder_1_out));  // open: cin, cout
  Register #(.width(64)) Cycle_Cnt (.D(adder_2_out), .en(1'b1), .clk(clock_1_out), .Q(Cycle_Cnt_q), .clr(button_1_out));
  Adder #(.width(64)) adder_2 (.a(Cycle_Cnt_q), .b(64'h1), .out(adder_2_out));  // open: cin, cout
  ROM #(.addrWidth(20), .dataWidth(32)) rom_1 (
    .addr(PC_q_2), .data({rom_1_data, rom_1_data_3[4], rom_1_data_2, rom_1_data_4}));
  Multiplexer #(.select(2), .width(32)) multiplexer_2 (
    .in0({adder_3_out_3, adder_3_out_2, adder_3_out}), .in1(adder_1_out), .in2({rom_1_data, {12{1'b0}}}),
    .in3(multiplexer_6_out), .out(multiplexer_2_out), .sel(or_3_out));
  Multiplexer #(.width(12)) multiplexer_3 (
    .in0(rom_1_data[31:20]), .in1({rom_1_data[31:25], rom_1_data_3[4], rom_1_data_2}),
    .out(multiplexer_3_out), .sel(or_2_out));
  minirv_GPR minirv_gpr_1 (
    .clk(clock_1_out), .wdata(multiplexer_2_out), .waddr(rom_1_data_2), .wEN(not_1_out),
    .rs1(rom_1_data[18:15]), .RST(button_1_out), .rs2(rom_1_data[23:20]), .rdata1(minirv_gpr_1_rdata1),
    .rdata2({minirv_gpr_1_rdata2, minirv_gpr_1_rdata2_2}));
  is_addi is_addi_1 (.OP(rom_1_data_4), .F3(rom_1_data[14:12]), .true(is_addi_1_true));
  is_jalr is_jalr_1 (.OP(rom_1_data_4), .F3(rom_1_data[14:12]), .true(is_jalr_1_true));
  is_add is_add_1 (.OP(rom_1_data_4), .F3(rom_1_data[14:12]), .F7(rom_1_data[31:25]));  // open: true
  is_lui is_lui_1 (.OP(rom_1_data_4), .true(is_lui_1_true));
  is_lw is_lw_1 (.OP(rom_1_data_4), .F3(rom_1_data[14:12]), .true(is_lw_1_true));
  is_sw is_sw_1 (.OP(rom_1_data_4), .F3(rom_1_data[14:12]), .true(is_sw_1_true));
  is_lbu is_lbu_1 (.OP(rom_1_data_4), .F3(rom_1_data[14:12]), .true(is_lbu_1_true));
  is_sb is_sb_1 (.OP(rom_1_data_4), .F3(rom_1_data[14:12]), .true(is_sb_1_true));
  // Probe on undriven
  Multiplexer #(.width(32)) multiplexer_4 (
    .in0({minirv_gpr_1_rdata2, minirv_gpr_1_rdata2_2}), .in1(bit_extender_1_out), .out(multiplexer_4_out),
    .sel(or_1_out));
  assign bit_extender_1_out = {{20{multiplexer_3_out[11]}}, multiplexer_3_out};  // Bit_Extender bit_extender_1
  not not_1 (not_1_out, or_2_out);
  Adder #(.width(32)) adder_3 (
    .a(minirv_gpr_1_rdata1), .b(multiplexer_4_out), .out({adder_3_out_3, adder_3_out_2, adder_3_out}));  // open: cin, cout
  or or_1 (or_1_out, is_addi_1_true, is_lbu_1_true, is_sb_1_true, is_sw_1_true, is_lw_1_true);
  or or_2 (or_2_out, is_sw_1_true, is_sb_1_true);
  or or_3 (or_3_out[0], is_jalr_1_true, is_lbu_1_true, is_lw_1_true);
  or or_4 (or_3_out[1], is_lw_1_true, is_lbu_1_true, is_lui_1_true);
  Decoder #(.select(2)) decoder_1 (
    .out0(decoder_1_out0), .out1(decoder_1_out1), .out2(decoder_1_out2), .out3(decoder_1_out3),
    .sel(adder_3_out));  // open: en
  RAM #(.addrWidth(20), .asyncread("true"), .byteenables("byteEnables"), .dataWidth(32), .\type ("nonvolatile")) ram_1 (
    .addr(adder_3_out_2), .we(or_2_out), .oe(1'b1), .clk(clock_1_out), .din(multiplexer_5_out),
    .dout({ram_1_dout_4, ram_1_dout_3, ram_1_dout_2, ram_1_dout}), .be3(or_8_out), .be2(or_7_out),
    .be1(or_6_out), .be0(or_5_out));
  Multiplexer #(.width(32)) multiplexer_5 (
    .in0({minirv_gpr_1_rdata2, minirv_gpr_1_rdata2_2}),
    .in1({minirv_gpr_1_rdata2_2, minirv_gpr_1_rdata2_2, minirv_gpr_1_rdata2_2, minirv_gpr_1_rdata2_2}),
    .out(multiplexer_5_out), .sel(is_sb_1_true));
  or or_5 (or_5_out, is_sw_1_true, decoder_1_out0);
  or or_6 (or_6_out, is_sw_1_true, decoder_1_out1);
  or or_7 (or_7_out, decoder_1_out2, is_sw_1_true);
  or or_8 (or_8_out, decoder_1_out3, is_sw_1_true);
  Multiplexer #(.width(32)) multiplexer_6 (
    .in0({ram_1_dout_4, ram_1_dout_3, ram_1_dout_2, ram_1_dout}), .in1(bit_extender_2_out),
    .out(multiplexer_6_out), .sel(is_lbu_1_true));
  assign bit_extender_2_out = {{24{1'b0}}, multiplexer_7_out};  // Bit_Extender bit_extender_2
  Multiplexer #(.select(2), .width(8)) multiplexer_7 (
    .in0(ram_1_dout), .in1(ram_1_dout_2), .in2(ram_1_dout_3), .in3(ram_1_dout_4), .out(multiplexer_7_out),
    .sel(adder_3_out));

  // Notes on the sheet:
  //   contents of rom_1 (hex, n*v repeats v):
  //   413 52137 10113 10b7 22408093 80e7 fea12823 fe812e23 1437 40840413 ff014183 3401b3 1c183 ff114203
  //   440233 24203 4181b3 ff214203 440233 24203 4181b3 ff314203 440233 24203 4181b3 1237 40020213 320233
  //   24203 ffc12403 420233 420233 410233 a000193 fe312823 9c00193 fe312623 fec22203 20067 8067 ff410113
  //   100513 112423 10b7 21808093 80e7 fec10113 912423 494b7 6b048493 812623 112823 496b7 69068693 48413
  //   48713 fe012823 174183 fe3109a3 ff012183 fe812e23 fe312823 3d437 60040413 ff214203 420233 420233
  //   440233 22203 fe412623 ff114203 420233 420233 440233 22203 fe412423 ff014203 420233 420233 440233
  //   22203 fe412223 fed14183 fea14203 4181b3 fe714203 4181b3 fe312223 fee14183 feb14203 4181b3 fe3102a3
  //   fef14183 fe310323 fe412183 8237 20213 440433 ff314203 420233 420233 440233 22203 ffc12403 4181b3
  //   74503 350533 6a603 270713 468693 fe312a23 fec12423 31237 50020213 feb14183 4181b3 1c183 fe3103a3
  //   fea14183 4181b3 1c183 fe310323 fe914183 4181b3 1c183 fe3102a3 fe814183 4181b3 1c183 fe310223
  //   ff412183 fe412203 450533 150513 fea12823 fe812e23 1437 40840413 ff014183 3401b3 1c183 ff114203
  //   440233 24203 4181b3 ff214203 440233 24203 4181b3 ff314203 440233 24203 4181b3 1237 40020213 320233
  //   24503 ffc12403 e12223 d12023 1800093 80e7 412703 497b7 6c078793 12683 fee12823 fef12623 fe812e23
  //   fe912c23 1437 30040413 ff014183 340233 100193 320023 fec14183 3401b3 18023 24183 ff114483 940233
  //   100493 920023 fed14483 9404b3 48023 24483 9181b3 ff214483 940233 100493 920023 fee14483 9404b3 48023
  //   24483 9181b3 ff314483 940233 100493 920023 fef14483 9404b3 48023 24483 9181b3 1237 40020213 320233
  //   24203 ff812483 ffc12403 420233 420233 410233 37800193 fe312823 e000193 fe312623 fec22203 20067 49737
  //   67070713 72683 fe012823 14c203 fe4108a3 ff012203 4c503 450533 470713 e12023 fe312a23 fed12423 31237
  //   50020213 feb14183 4181b3 1c183 fe3103a3 fea14183 4181b3 1c183 fe310323 fe914183 4181b3 1c183
  //   fe3102a3 fe814183 4181b3 1c183 fe310223 ff412183 fe412203 450533 150513 fea12823 fe812e23 1437
  //   40840413 ff014183 3401b3 1c183 ff114203 440233 24203 4181b3 ff214203 440233 24203 4181b3 ff314203
  //   440233 24203 4181b3 1237 40020213 320233 24503 ffc12403 1800093 80e7 248493 497b7 6c078793 12703
  //   fe912823 fef12623 fe812e23 fe912c23 1437 30040413 ff014183 340233 100193 320023 fec14183 3401b3
  //   18023 24183 ff114483 940233 100493 920023 fed14483 9404b3 48023 24483 9181b3 ff214483 940233 100493
  //   920023 fee14483 9404b3 48023 24483 9181b3 ff314483 940233 100493 920023 fef14483 9404b3 48023 24483
  //   9181b3 1237 40020213 320233 24203 ff812483 ffc12403 420233 420233 410233 55c00193 fe312823 38000193
  //   fe312623 fec22203 20067 244683 144603 344703 444783 494b7 64048493 8*d686b3 fed12823 fec12623 116b7
  //   60068693 fe012223 ff314203 fe4102a3 fef14203 fe410223 fe412203 468233 24203 fe4105a3 ff214203
  //   fe4102a3 fee14203 fe410223 fe412203 468233 24203 fe410523 ff114203 fe4102a3 fed14203 fe410223
  //   fe412203 468233 24203 fe4104a3 ff014203 fe4102a3 fec14203 fe410223 fe412203 468233 24203 fe410423
  //   fe812683 4a503 fe012823 fee10923 fee12423 fe914203 fe4109a3 ff012703 fee12823 fed12623 11737
  //   60070713 fe012223 ff314203 fe4102a3 fef14203 fe410223 fe412203 470233 24203 fe4105a3 ff214203
  //   fe4102a3 fee14203 fe410223 fe412203 470233 24203 fe410523 ff114203 fe4102a3 fed14203 fe410223
  //   fe412203 470233 24203 fe4104a3 ff014203 fe4102a3 fec14203 fe410223 fe412203 470233 24203 fe410423
  //   fe812703 fe012823 fef109a3 ff012783 fef12823 fee12623 117b7 60078793 fe012223 ff314203 fe4102a3
  //   fef14203 fe410223 fe412203 478233 24203 fe4105a3 ff214203 fe4102a3 fee14203 fe410223 fe412203 478233
  //   24203 fe410523 ff114203 fe4102a3 fed14203 fe410223 fe412203 478233 24203 fe4104a3 ff014203 fe4102a3
  //   fec14203 fe410223 fe412203 478233 24203 fe410423 fe812783 fe312a23 fef12423 31237 50020213 feb14183
  //   4181b3 1c183 fe3103a3 fea14183 4181b3 1c183 fe310323 fe914183 4181b3 1c183 fe3102a3 fe814183 4181b3
  //   1c183 fe310223 ff412183 fe412203 450533 150513 fea12823 fe812e23 1437 40840413 ff014183 3401b3 1c183
  //   ff114203 440233 24203 4181b3 ff214203 440233 24203 4181b3 ff314203 440233 24203 4181b3 1237 400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
endmodule

module minirv_GPR (
  input  clk,
  input  [31:0] wdata,
  input  [3:0] waddr,
  input  wEN,
  input  [3:0] rs1,
  input  RST,
  input  [3:0] rs2,
  output [31:0] rdata1,
  output [31:0] rdata2
);

  wire decoder_1_out1, decoder_1_out2, decoder_1_out3, decoder_1_out4, decoder_1_out5, decoder_1_out6,
       decoder_1_out7, decoder_1_out8, decoder_1_out9, decoder_1_out10, decoder_1_out11, decoder_1_out12,
       decoder_1_out13, decoder_1_out14, decoder_1_out15;
  wire [31:0] register_1_q, register_2_q, register_3_q, register_4_q, register_5_q, register_6_q,
       register_7_q, register_8_q, register_9_q, register_10_q, register_11_q, register_12_q, register_13_q,
       register_14_q, register_15_q, register_16_q;

  Decoder #(.select(4)) decoder_1 (
    .out1(decoder_1_out1), .out2(decoder_1_out2), .out3(decoder_1_out3), .out4(decoder_1_out4),
    .out5(decoder_1_out5), .out6(decoder_1_out6), .out7(decoder_1_out7), .out8(decoder_1_out8),
    .out9(decoder_1_out9), .out10(decoder_1_out10), .out11(decoder_1_out11), .out12(decoder_1_out12),
    .out13(decoder_1_out13), .out14(decoder_1_out14), .out15(decoder_1_out15), .sel(waddr), .en(wEN));  // open: out0
  Register #(.width(32)) register_1 (.D(wdata), .en(1'b0), .clk(clk), .Q(register_1_q), .clr(RST));
  Register #(.width(32)) register_2 (.D(wdata), .en(decoder_1_out8), .clk(clk), .Q(register_2_q), .clr(RST));
  Register #(.width(32)) register_3 (.D(wdata), .en(decoder_1_out1), .clk(clk), .Q(register_3_q), .clr(RST));
  Register #(.width(32)) register_4 (.D(wdata), .en(decoder_1_out9), .clk(clk), .Q(register_4_q), .clr(RST));
  Register #(.width(32)) register_5 (.D(wdata), .en(decoder_1_out2), .clk(clk), .Q(register_5_q), .clr(RST));
  Register #(.width(32)) register_6 (.D(wdata), .en(decoder_1_out10), .clk(clk), .Q(register_6_q), .clr(RST));
  Register #(.width(32)) register_7 (.D(wdata), .en(decoder_1_out3), .clk(clk), .Q(register_7_q), .clr(RST));
  Register #(.width(32)) register_8 (.D(wdata), .en(decoder_1_out11), .clk(clk), .Q(register_8_q), .clr(RST));
  Register #(.width(32)) register_9 (.D(wdata), .en(decoder_1_out4), .clk(clk), .Q(register_9_q), .clr(RST));
  Register #(.width(32)) register_10 (.D(wdata), .en(decoder_1_out12), .clk(clk), .Q(register_10_q), .clr(RST));
  Register #(.width(32)) register_11 (.D(wdata), .en(decoder_1_out5), .clk(clk), .Q(register_11_q), .clr(RST));
  Register #(.width(32)) register_12 (.D(wdata), .en(decoder_1_out13), .clk(clk), .Q(register_12_q), .clr(RST));
  Register #(.width(32)) register_13 (.D(wdata), .en(decoder_1_out6), .clk(clk), .Q(register_13_q), .clr(RST));
  Register #(.width(32)) register_14 (.D(wdata), .en(decoder_1_out14), .clk(clk), .Q(register_14_q), .clr(RST));
  Register #(.width(32)) register_15 (.D(wdata), .en(decoder_1_out7), .clk(clk), .Q(register_15_q), .clr(RST));
  Register #(.width(32)) register_16 (.D(wdata), .en(decoder_1_out15), .clk(clk), .Q(register_16_q), .clr(RST));
  Multiplexer #(.select(4), .width(32)) multiplexer_1 (
    .in0(register_1_q), .in1(register_3_q), .in2(register_5_q), .in3(register_7_q), .in4(register_9_q),
    .in5(register_11_q), .in6(register_13_q), .in7(register_15_q), .in8(register_2_q), .in9(register_4_q),
    .in10(register_6_q), .in11(register_8_q), .in12(register_10_q), .in13(register_12_q),
    .in14(register_14_q), .in15(register_16_q), .out(rdata1), .sel(rs1));
  Multiplexer #(.select(4), .width(32)) multiplexer_2 (
    .in0(register_1_q), .in1(register_3_q), .in2(register_5_q), .in3(register_7_q), .in4(register_9_q),
    .in5(register_11_q), .in6(register_13_q), .in7(register_15_q), .in8(register_2_q), .in9(register_4_q),
    .in10(register_6_q), .in11(register_8_q), .in12(register_10_q), .in13(register_12_q),
    .in14(register_14_q), .in15(register_16_q), .out(rdata2), .sel(rs2));
endmodule

module is_addi (
  input  [6:0] OP,
  input  [2:0] F3,
  output true
);

  wire comparator_1_eq, comparator_2_eq;

  Comparator #(.mode("unsigned"), .width(7)) comparator_1 (
    .a(OP), .b(7'b0010011), .eq(comparator_1_eq));  // open: gt, lt
  Comparator #(.mode("unsigned"), .width(3)) comparator_2 (.a(F3), .b(3'b000), .eq(comparator_2_eq));  // open: gt, lt
  and and_1 (true, comparator_1_eq, comparator_2_eq);
endmodule

module is_jalr (
  input  [6:0] OP,
  input  [2:0] F3,
  output true
);

  wire comparator_1_eq, comparator_2_eq;

  Comparator #(.mode("unsigned"), .width(7)) comparator_1 (
    .a(OP), .b(7'b1100111), .eq(comparator_1_eq));  // open: gt, lt
  Comparator #(.mode("unsigned"), .width(3)) comparator_2 (.a(F3), .b(3'b000), .eq(comparator_2_eq));  // open: gt, lt
  and and_1 (true, comparator_1_eq, comparator_2_eq);
endmodule

module is_add (
  input  [6:0] OP,
  input  [2:0] F3,
  input  [6:0] F7,
  output true
);

  wire comparator_1_eq, comparator_2_eq, comparator_3_eq;

  Comparator #(.mode("unsigned"), .width(7)) comparator_1 (
    .a(OP), .b(7'b0110011), .eq(comparator_1_eq));  // open: gt, lt
  Comparator #(.mode("unsigned"), .width(3)) comparator_2 (.a(F3), .b(3'b000), .eq(comparator_2_eq));  // open: gt, lt
  Comparator #(.mode("unsigned"), .width(7)) comparator_3 (
    .a(F7), .b({7{1'b0}}), .eq(comparator_3_eq));  // open: gt, lt
  and and_1 (true, comparator_1_eq, comparator_2_eq, comparator_3_eq);
endmodule

module is_lui (
  input  [6:0] OP,
  output true
);

  Comparator #(.mode("unsigned"), .width(7)) comparator_1 (.a(OP), .b(7'b0110111), .eq(true));  // open: gt, lt
endmodule

module is_lw (
  input  [6:0] OP,
  input  [2:0] F3,
  output true
);

  wire comparator_1_eq, comparator_2_eq;

  Comparator #(.mode("unsigned"), .width(7)) comparator_1 (
    .a(OP), .b(7'b0000011), .eq(comparator_1_eq));  // open: gt, lt
  Comparator #(.mode("unsigned"), .width(3)) comparator_2 (.a(F3), .b(3'b010), .eq(comparator_2_eq));  // open: gt, lt
  and and_1 (true, comparator_1_eq, comparator_2_eq);
endmodule

module is_sw (
  input  [6:0] OP,
  input  [2:0] F3,
  output true
);

  wire comparator_1_eq, comparator_2_eq;

  Comparator #(.mode("unsigned"), .width(7)) comparator_1 (
    .a(OP), .b(7'b0100011), .eq(comparator_1_eq));  // open: gt, lt
  Comparator #(.mode("unsigned"), .width(3)) comparator_2 (.a(F3), .b(3'b010), .eq(comparator_2_eq));  // open: gt, lt
  and and_1 (true, comparator_1_eq, comparator_2_eq);
endmodule

module is_lbu (
  input  [6:0] OP,
  input  [2:0] F3,
  output true
);

  wire comparator_1_eq, comparator_2_eq;

  Comparator #(.mode("unsigned"), .width(7)) comparator_1 (
    .a(OP), .b(7'b0000011), .eq(comparator_1_eq));  // open: gt, lt
  Comparator #(.mode("unsigned"), .width(3)) comparator_2 (.a(F3), .b(3'b100), .eq(comparator_2_eq));  // open: gt, lt
  and and_1 (true, comparator_1_eq, comparator_2_eq);
endmodule

module is_sb (
  input  [6:0] OP,
  input  [2:0] F3,
  output true
);

  wire comparator_1_eq, comparator_2_eq;

  Comparator #(.mode("unsigned"), .width(7)) comparator_1 (
    .a(OP), .b(7'b0100011), .eq(comparator_1_eq));  // open: gt, lt
  Comparator #(.mode("unsigned"), .width(3)) comparator_2 (.a(F3), .b(3'b000), .eq(comparator_2_eq));  // open: gt, lt
  and and_1 (true, comparator_1_eq, comparator_2_eq);
endmodule
