// Logisim project minirv_addi_jalr.circ as structural Verilog: 4 circuits, main circuit main
module main (
);

  wire button_1_out, clock_1_out, is_addi_1_true, is_jalr_1_true, or_1_out;
  wire [2:0] rom_1_data_4;
  wire [3:0] rom_1_data_2, rom_1_data_5, rom_1_data_6;
  wire [6:0] rom_1_data;
  wire [7:0] PC_q_2;
  wire [31:0] adder_1_out, adder_2_out, bit_extender_1_out, minirv_gpr_1_rdata1, multiplexer_1_out,
       multiplexer_2_out, PC_q;
  wire [31:11] rom_1_data_3;

  Clock clock_1 (.out(clock_1_out));
  Multiplexer #(.width(32)) multiplexer_1 (
    .in0(adder_1_out), .in1(adder_2_out), .out(multiplexer_1_out), .sel(is_jalr_1_true));
  Register #(.width(32)) PC (
    .D(multiplexer_1_out), .en(1'b1), .clk(clock_1_out), .Q({PC_q[31:10], PC_q_2, PC_q[1:0]}),
    .clr(button_1_out));
  Button button_1 (.out(button_1_out));
  Adder #(.width(32)) adder_1 (.a({PC_q[31:10], PC_q_2, PC_q[1:0]}), .b(32'h4), .out(adder_1_out));  // open: cin, cout
  ROM #(.dataWidth(32)) rom_1 (
    .addr(PC_q_2),
    .data({rom_1_data_3[31:24], rom_1_data_6, rom_1_data_3[19], rom_1_data_5, rom_1_data_4, rom_1_data_3[11], rom_1_data_2, rom_1_data}));
  Multiplexer #(.width(32)) multiplexer_2 (
    .in0(adder_2_out), .in1(adder_1_out), .out(multiplexer_2_out), .sel(is_jalr_1_true));
  // Probe on multiplexer_2_out
  minirv_GPR minirv_gpr_1 (
    .clk(clock_1_out), .wdata(multiplexer_2_out), .waddr(rom_1_data_2), .wEN(or_1_out), .rs1(rom_1_data_5),
    .rs2(rom_1_data_6), .rdata1(minirv_gpr_1_rdata1));  // open: rdata2
  is_addi is_addi_1 (.OP(rom_1_data), .F3(rom_1_data_4), .true(is_addi_1_true));
  is_jalr is_jalr_1 (.OP(rom_1_data), .F3(rom_1_data_4), .true(is_jalr_1_true));
  or or_1 (or_1_out, is_addi_1_true, is_jalr_1_true);
  Adder #(.width(32)) adder_2 (.a(minirv_gpr_1_rdata1), .b(bit_extender_1_out), .out(adder_2_out));  // open: cin, cout
  assign bit_extender_1_out = {{20{rom_1_data_3[31]}}, {rom_1_data_3[31:24], rom_1_data_6}};  // Bit_Extender bit_extender_1

  // Notes on the sheet:
  //   contents of rom_1 (hex, n*v repeats v):
  //   1400513 10000e7 c000e7 c00067 a50513 8067
endmodule

module minirv_GPR (
  input  clk,
  input  [31:0] wdata,
  input  [3:0] waddr,
  input  wEN,
  input  [3:0] rs1,
  input  [3:0] rs2,
  output [31:0] rdata1,
  output [31:0] rdata2
);

  wire decoder_1_out1, decoder_1_out2, decoder_1_out3, decoder_1_out4, decoder_1_out5, decoder_1_out6,
       decoder_1_out7, decoder_1_out8, decoder_1_out9, decoder_1_out10, decoder_1_out11, decoder_1_out12,
       decoder_1_out13, decoder_1_out14, decoder_1_out15;
  wire [31:0] register_1_q, register_2_q, register_3_q, register_4_q, register_5_q, register_6_q,
       register_7_q, register_8_q, register_9_q, register_10_q, register_11_q, register_12_q, register_13_q,
       register_14_q, register_15_q, register_16_q;

  Decoder #(.select(4)) decoder_1 (
    .out1(decoder_1_out1), .out2(decoder_1_out2), .out3(decoder_1_out3), .out4(decoder_1_out4),
    .out5(decoder_1_out5), .out6(decoder_1_out6), .out7(decoder_1_out7), .out8(decoder_1_out8),
    .out9(decoder_1_out9), .out10(decoder_1_out10), .out11(decoder_1_out11), .out12(decoder_1_out12),
    .out13(decoder_1_out13), .out14(decoder_1_out14), .out15(decoder_1_out15), .sel(waddr), .en(wEN));  // open: out0
  Register #(.width(32)) register_1 (.D(wdata), .en(1'b0), .clk(clk), .Q(register_1_q));  // open: clr
  Register #(.width(32)) register_2 (.D(wdata), .en(decoder_1_out8), .clk(clk), .Q(register_2_q));  // open: clr
  Register #(.width(32)) register_3 (.D(wdata), .en(decoder_1_out1), .clk(clk), .Q(register_3_q));  // open: clr
  Register #(.width(32)) register_4 (.D(wdata), .en(decoder_1_out9), .clk(clk), .Q(register_4_q));  // open: clr
  Register #(.width(32)) register_5 (.D(wdata), .en(decoder_1_out2), .clk(clk), .Q(register_5_q));  // open: clr
  Register #(.width(32)) register_6 (.D(wdata), .en(decoder_1_out10), .clk(clk), .Q(register_6_q));  // open: clr
  Register #(.width(32)) register_7 (.D(wdata), .en(decoder_1_out3), .clk(clk), .Q(register_7_q));  // open: clr
  Register #(.width(32)) register_8 (.D(wdata), .en(decoder_1_out11), .clk(clk), .Q(register_8_q));  // open: clr
  Register #(.width(32)) register_9 (.D(wdata), .en(decoder_1_out4), .clk(clk), .Q(register_9_q));  // open: clr
  Register #(.width(32)) register_10 (.D(wdata), .en(decoder_1_out12), .clk(clk), .Q(register_10_q));  // open: clr
  Register #(.width(32)) register_11 (.D(wdata), .en(decoder_1_out5), .clk(clk), .Q(register_11_q));  // open: clr
  Register #(.width(32)) register_12 (.D(wdata), .en(decoder_1_out13), .clk(clk), .Q(register_12_q));  // open: clr
  Register #(.width(32)) register_13 (.D(wdata), .en(decoder_1_out6), .clk(clk), .Q(register_13_q));  // open: clr
  Register #(.width(32)) register_14 (.D(wdata), .en(decoder_1_out14), .clk(clk), .Q(register_14_q));  // open: clr
  Register #(.width(32)) register_15 (.D(wdata), .en(decoder_1_out7), .clk(clk), .Q(register_15_q));  // open: clr
  Register #(.width(32)) register_16 (.D(wdata), .en(decoder_1_out15), .clk(clk), .Q(register_16_q));  // open: clr
  Multiplexer #(.select(4), .width(32)) multiplexer_1 (
    .in0(register_1_q), .in1(register_3_q), .in2(register_5_q), .in3(register_7_q), .in4(register_9_q),
    .in5(register_11_q), .in6(register_13_q), .in7(register_15_q), .in8(register_2_q), .in9(register_4_q),
    .in10(register_6_q), .in11(register_8_q), .in12(register_10_q), .in13(register_12_q),
    .in14(register_14_q), .in15(register_16_q), .out(rdata1), .sel(rs1));
  Multiplexer #(.select(4), .width(32)) multiplexer_2 (
    .in0(register_1_q), .in1(register_3_q), .in2(register_5_q), .in3(register_7_q), .in4(register_9_q),
    .in5(register_11_q), .in6(register_13_q), .in7(register_15_q), .in8(register_2_q), .in9(register_4_q),
    .in10(register_6_q), .in11(register_8_q), .in12(register_10_q), .in13(register_12_q),
    .in14(register_14_q), .in15(register_16_q), .out(rdata2), .sel(rs2));
endmodule

module is_addi (
  input  [6:0] OP,
  input  [2:0] F3,
  output true
);

  wire comparator_1_eq, comparator_2_eq;

  Comparator #(.mode("unsigned"), .width(7)) comparator_1 (
    .a(OP), .b(7'b0010011), .eq(comparator_1_eq));  // open: gt, lt
  Comparator #(.mode("unsigned"), .width(3)) comparator_2 (.a(F3), .b(3'b000), .eq(comparator_2_eq));  // open: gt, lt
  and and_1 (true, comparator_1_eq, comparator_2_eq);
endmodule

module is_jalr (
  input  [6:0] OP,
  input  [2:0] F3,
  output true
);

  wire comparator_1_eq, comparator_2_eq;

  Comparator #(.mode("unsigned"), .width(7)) comparator_1 (
    .a(OP), .b(7'b1100111), .eq(comparator_1_eq));  // open: gt, lt
  Comparator #(.mode("unsigned"), .width(3)) comparator_2 (.a(F3), .b(3'b000), .eq(comparator_2_eq));  // open: gt, lt
  and and_1 (true, comparator_1_eq, comparator_2_eq);
endmodule
